// Logisim project reversi.circ as structural Verilog
module main (
);

  wire Bot_win__and_you_lose__if_you_don_t_understand, button_1_out, button_2_out, button_3_out,
       button_4_out, button_5_out, button_6_out, button_7_out, button_8_out, button_9_out, button_10_out,
       button_11_out, button_12_out, button_13_out, button_14_out, button_15_out, button_16_out,
       button_17_out, button_18_out, button_19_out, button_20_out, button_21_out, button_22_out,
       button_23_out, button_24_out, button_25_out, button_26_out, button_27_out, button_28_out,
       button_29_out, button_30_out, button_31_out, button_32_out, button_33_out, button_34_out,
       button_35_out, button_36_out, can, Draw, game_over, not_1_out, reset, start, The_game_is_on_or_not,
       turn, turnnowb, turnnoww, You_win;
  wire [2:0] row;
  wire [3:0] to_indicator_1_out_2, to_indicator_1_out_3, to_indicator_2_out_2, to_indicator_2_out_3;
  wire [5:0] _0, _1, _2, _3, _4, _5, column, registers_to_matrix_1_black_count, registers_to_matrix_1_out_6,
       registers_to_matrix_1_out_8, registers_to_matrix_1_out_10, registers_to_matrix_1_out_12,
       registers_to_matrix_1_out_14, registers_to_matrix_1_out_17, registers_to_matrix_1_white_count;
  wire [6:0] registers_to_matrix_1_out_7, registers_to_matrix_1_out_9, registers_to_matrix_1_out_11,
       registers_to_matrix_1_out_13, registers_to_matrix_1_out_16, registers_to_matrix_1_out_18;

  Button u_Start (.out(start));
  Button u_Reset (.out(reset));
  LED led_1 (.in(You_win));
  to_indicator to_indicator_1 (
    .in_1(registers_to_matrix_1_white_count), .out_2(to_indicator_1_out_2), .out_3(to_indicator_1_out_3));
  Hex_Digit_Display hex_digit_display_1 (.value(to_indicator_1_out_2));  // open: dp
  registers_to_matrix registers_to_matrix_1 (
    .in_4(column), .out_7(registers_to_matrix_1_out_7), .out_9(registers_to_matrix_1_out_9),
    .out_11(registers_to_matrix_1_out_11), .in_5(row), .out_13(registers_to_matrix_1_out_13),
    .out_16(registers_to_matrix_1_out_16), .out_18(registers_to_matrix_1_out_18),
    .out_6(registers_to_matrix_1_out_6), .out_8(registers_to_matrix_1_out_8),
    .out_10(registers_to_matrix_1_out_10), .out_12(registers_to_matrix_1_out_12),
    .out_14(registers_to_matrix_1_out_14), .out_17(registers_to_matrix_1_out_17), .in_2(turn), .in_1(start),
    .white_count(registers_to_matrix_1_white_count), .black_count(registers_to_matrix_1_black_count),
    .in_3(reset), .out_15(can), .out_21(game_over), .out_22(You_win),
    .out_23(Bot_win__and_you_lose__if_you_don_t_understand), .out_24(Draw));
  DotMatrix #(.inputtype("row"), .matrixcols(6), .matrixrows(6), .dotshape("circle")) dotmatrix_1 (
    .row0(registers_to_matrix_1_out_6), .row1(registers_to_matrix_1_out_8),
    .row2(registers_to_matrix_1_out_10), .row3(registers_to_matrix_1_out_12),
    .row4(registers_to_matrix_1_out_14), .row5(registers_to_matrix_1_out_17));
  DotMatrix #(.inputtype("row"), .matrixcols(7), .matrixrows(6), .dotshape("circle")) dotmatrix_2 (
    .row0(registers_to_matrix_1_out_7), .row1(registers_to_matrix_1_out_9),
    .row2(registers_to_matrix_1_out_11), .row3(registers_to_matrix_1_out_13),
    .row4(registers_to_matrix_1_out_16), .row5(registers_to_matrix_1_out_18));
  Hex_Digit_Display hex_digit_display_2 (.value(to_indicator_1_out_3));  // open: dp
  LED led_2 (.in(The_game_is_on_or_not));
  Button button_1 (.out(button_1_out));
  Button button_2 (.out(button_2_out));
  Button button_3 (.out(button_3_out));
  Button button_4 (.out(button_4_out));
  Button button_5 (.out(button_5_out));
  Button button_6 (.out(button_6_out));
  LED Your_move (.in(turnnoww));
  LED led_3 (.in(Draw));
  to_indicator to_indicator_2 (
    .in_1(registers_to_matrix_1_black_count), .out_2(to_indicator_2_out_2), .out_3(to_indicator_2_out_3));
  Hex_Digit_Display hex_digit_display_3 (.value(to_indicator_2_out_2));  // open: dp
  Button button_7 (.out(button_7_out));
  Button button_8 (.out(button_8_out));
  Button button_9 (.out(button_9_out));
  Button button_10 (.out(button_10_out));
  Button button_11 (.out(button_11_out));
  Button button_12 (.out(button_12_out));
  Button button_13 (.out(button_13_out));
  Button button_14 (.out(button_14_out));
  Button button_15 (.out(button_15_out));
  Button button_16 (.out(button_16_out));
  Button button_17 (.out(button_17_out));
  Button button_18 (.out(button_18_out));
  Button button_19 (.out(button_19_out));
  Button button_20 (.out(button_20_out));
  Button button_21 (.out(button_21_out));
  Button button_22 (.out(button_22_out));
  Button button_23 (.out(button_23_out));
  Button button_24 (.out(button_24_out));
  Button button_25 (.out(button_25_out));
  Button button_26 (.out(button_26_out));
  Button button_27 (.out(button_27_out));
  Button button_28 (.out(button_28_out));
  Button button_29 (.out(button_29_out));
  Button button_30 (.out(button_30_out));
  LED led_4 (.in(Bot_win__and_you_lose__if_you_don_t_understand));
  Hex_Digit_Display hex_digit_display_4 (.value(to_indicator_2_out_3));  // open: dp
  Button button_31 (.out(button_31_out));
  buttons_row buttons_row_1 (
    .in_1(button_1_out), .in_2(button_8_out), .in_3(button_10_out), .in_4(button_9_out), .in_5(button_7_out),
    .in_6(button_31_out), .out_7(_0));
  buttons_row buttons_row_2 (
    .in_1(button_2_out), .in_2(button_12_out), .in_3(button_11_out), .in_4(button_13_out),
    .in_5(button_14_out), .in_6(button_32_out), .out_7(_1));
  Button button_32 (.out(button_32_out));
  Button button_33 (.out(button_33_out));
  buttons_row buttons_row_3 (
    .in_1(button_3_out), .in_2(button_15_out), .in_3(button_17_out), .in_4(button_16_out),
    .in_5(button_18_out), .in_6(button_33_out), .out_7(_2));
  buttons_row buttons_row_4 (
    .in_1(button_4_out), .in_2(button_21_out), .in_3(button_19_out), .in_4(button_22_out),
    .in_5(button_20_out), .in_6(button_34_out), .out_7(_3));
  Button button_34 (.out(button_34_out));
  Button button_35 (.out(button_35_out));
  buttons_row buttons_row_5 (
    .in_1(button_5_out), .in_2(button_26_out), .in_3(button_25_out), .in_4(button_23_out),
    .in_5(button_24_out), .in_6(button_35_out), .out_7(_4));
  buttons_row buttons_row_6 (
    .in_1(button_6_out), .in_2(button_28_out), .in_3(button_30_out), .in_4(button_29_out),
    .in_5(button_27_out), .in_6(button_36_out), .out_7(_5));
  Button button_36 (.out(button_36_out));
  LED The_bot_s_move (.in(turnnowb));
  and and_1 (turnnoww, not_1_out, The_game_is_on_or_not);
  not not_1 (not_1_out, turn);
  baza baza_1 (
    .in_3(_0), .in_6(_1), .in_7(_2), .in_8(_3), .in_9(_4), .in_10(_5), .this_is_the_row_number(row),
    .this_is_the_column_number(column), .The_player_s_turn__When_zero_is_white_s_move(turn), .can(can),
    .reset(reset), .start(start), .out_11(The_game_is_on_or_not), .game_over(game_over));
  and and_2 (turnnowb, turn, The_game_is_on_or_not);

  // Notes on the sheet:
  //   WHITE
  //   BLACK
endmodule

module baza (
  input  start,
  input  can,
  input  [5:0] in_3,
  input  game_over,
  input  reset,
  input  [5:0] in_6,
  input  [5:0] in_7,
  input  [5:0] in_8,
  input  [5:0] in_9,
  input  [5:0] in_10,
  output out_11,
  output The_player_s_turn__When_zero_is_white_s_move,
  output [2:0] this_is_the_row_number,
  output [5:0] this_is_the_column_number
);

  wire and_1_out, clock_1_out, clock_2_out, or_1_out, or_2_out, register_1_q, sw1, sw2, write;
  wire [2:0] row0, row1, row2, row3, row4, row5;
  wire [5:0] col0, col1, col2, col3, col4, col5;

  Clock clock_1 (.out(clock_1_out));
  row_selection row_selection_1 (
    .in_1(in_3[0]), .in_2(in_3[1]), .in_3(in_3[2]), .in_4(in_3[3]), .in_5(in_3[4]), .in_6(in_3[5]),
    .in_7(3'b000), .out_8(row0));
  row_selection row_selection_2 (
    .in_1(in_6[0]), .in_2(in_6[1]), .in_3(in_6[2]), .in_4(in_6[3]), .in_5(in_6[4]), .in_6(in_6[5]),
    .in_7(3'b001), .out_8(row1));
  row_selection row_selection_3 (
    .in_1(in_7[0]), .in_2(in_7[1]), .in_3(in_7[2]), .in_4(in_7[3]), .in_5(in_7[4]), .in_6(in_7[5]),
    .in_7(3'b010), .out_8(row2));
  Register #(.width(1)) u_start (.D(start), .en(start), .Q(out_11), .clk(clock_1_out), .clr(or_1_out));
  or or_1 (or_1_out, game_over, reset);
  row_selection row_selection_4 (
    .in_1(in_8[0]), .in_2(in_8[1]), .in_3(in_8[2]), .in_4(in_8[3]), .in_5(in_8[4]), .in_6(in_8[5]),
    .in_7(3'b011), .out_8(row3));
  row_selection row_selection_5 (
    .in_1(in_9[0]), .in_2(in_9[1]), .in_3(in_9[2]), .in_4(in_9[3]), .in_5(in_9[4]), .in_6(in_9[5]),
    .in_7(3'b100), .out_8(row4));
  row_selection row_selection_6 (
    .in_1(in_10[0]), .in_2(in_10[1]), .in_3(in_10[2]), .in_4(in_10[3]), .in_5(in_10[4]), .in_6(in_10[5]),
    .in_7(3'b101), .out_8(row5));
  or or_2 (or_2_out, in_3[0], in_3[1], in_3[2], in_3[3], in_3[4], in_3[5], in_6[0], in_6[1], in_6[2], in_6[3], in_6[4], in_6[5], in_7[0], in_7[1], in_7[2], in_7[3], in_7[4], in_7[5], in_8[0], in_8[1], in_8[2], in_8[3], in_8[4], in_8[5], in_9[0], in_9[1], in_9[2], in_9[3], in_9[4], in_9[5], in_10[0], in_10[1]);
  or or_3 (write, or_2_out, in_10[2], in_10[3], in_10[4], in_10[5]);
  column_selection column_selection_1 (
    .in_1(in_3[0]), .in_2(in_6[0]), .in_3(in_7[0]), .in_4(in_8[0]), .in_5(in_9[0]), .in_6(in_10[0]),
    .in_7(6'b000001), .out_8(col0));
  column_selection column_selection_2 (
    .in_1(in_3[2]), .in_2(in_6[2]), .in_3(in_7[2]), .in_4(in_8[2]), .in_5(in_9[2]), .in_6(in_10[2]),
    .in_7(6'b000100), .out_8(col2));
  column_selection column_selection_3 (
    .in_1(in_3[4]), .in_2(in_6[4]), .in_3(in_7[4]), .in_4(in_8[4]), .in_5(in_9[4]), .in_6(in_10[4]),
    .in_7(6'b010000), .out_8(col4));
  Pull_Resistor pull_resistor_1 (.node(can));
  and and_1 (and_1_out, write, out_11);
  switch_turn switch_turn_1 (.in_1(sw1), .\сама_кнопка (write), .in_3(sw2));  // open: out_4
  column_selection column_selection_4 (
    .in_1(in_3[1]), .in_2(in_6[1]), .in_3(in_7[1]), .in_4(in_8[1]), .in_5(in_9[1]), .in_6(in_10[1]),
    .in_7(6'b000010), .out_8(col1));
  column_selection column_selection_5 (
    .in_1(in_3[3]), .in_2(in_6[3]), .in_3(in_7[3]), .in_4(in_8[3]), .in_5(in_9[3]), .in_6(in_10[3]),
    .in_7(6'b001000), .out_8(col3));
  column_selection column_selection_6 (
    .in_1(in_3[5]), .in_2(in_6[5]), .in_3(in_7[5]), .in_4(in_8[5]), .in_5(in_9[5]), .in_6(in_10[5]),
    .in_7(6'b100000), .out_8(col5));
  Register #(.width(1)) register_1 (.D(can), .en(can), .Q(register_1_q), .clk(clock_2_out));  // open: clr
  Clock clock_2 (.out(clock_2_out));
  T_Flip_Flop t_ff_1 (
    .clk(and_1_out), .T(and_1_out), .Q(The_player_s_turn__When_zero_is_white_s_move), .reset(or_1_out));  // open: Qn, preset, en
  assign this_is_the_row_number = row0 & row1 & row2 & row3 & row4 & row5;  // AND_Gate and_2, 3 bits wide
  assign this_is_the_column_number = col0 | col1 | col2 | col3 | col4 | col5;  // OR_Gate or_4, 6 bits wide

  // Other names for the same wires on the sheet: game_play = out_11; _00 = in_3[0]; _10 = in_3[1]; _20 = in_3[2];
  //   _30 = in_3[3]; _40 = in_3[4]; _50 = in_3[5]; _01 = in_6[0]; _11 = in_6[1]; _21 = in_6[2]; _31 = in_6[3];
  //   _41 = in_6[4]; _51 = in_6[5]; _02 = in_7[0]; _12 = in_7[1]; _22 = in_7[2]; _32 = in_7[3]; _42 = in_7[4];
  //   _52 = in_7[5]; _03 = in_8[0]; _13 = in_8[1]; _23 = in_8[2]; _33 = in_8[3]; _43 = in_8[4]; _53 = in_8[5];
  //   _04 = in_9[0]; _14 = in_9[1]; _24 = in_9[2]; _34 = in_9[3]; _44 = in_9[4]; _54 = in_9[5]; _05 = in_10[0];
  //   _15 = in_10[1]; _25 = in_10[2]; _35 = in_10[3]; _45 = in_10[4]; _55 = in_10[5]
endmodule

module registers_to_matrix (
  input  in_1,
  input  in_2,
  input  in_3,
  input  [5:0] in_4,
  input  [2:0] in_5,
  output [5:0] out_6,
  output [6:0] out_7,
  output [5:0] out_8,
  output [6:0] out_9,
  output [5:0] out_10,
  output [6:0] out_11,
  output [5:0] out_12,
  output [6:0] out_13,
  output [5:0] out_14,
  output out_15,
  output [6:0] out_16,
  output [5:0] out_17,
  output [6:0] out_18,
  output [5:0] white_count,
  output [5:0] black_count,
  output out_21,
  output out_22,
  output out_23,
  output out_24
);

  wire _1, _2, _3, _4, _5, _6, and_2_out, and_3_out, and_5_out, and_6_out, and_8_out, and_9_out, and_10_out,
       and_11_out, and_13_out, and_14_out, and_16_out, and_17_out, and_19_out, and_20_out, and_22_out,
       and_24_out, bot_move, can_w1, can_w2, can_w3, can_w4, can_w5, can_w6, compare_6bit_1_out_3,
       compare_6bit_2_out_3, do_diag_coloring_3, do_diag_coloring_4, ld_diag, lu_diag, not_1_out, not_2_out,
       not_3_out, not_4_out, or_7_out, or_8_out, or_9_out, or_10_out, or_11_out, or_12_out, or_23_out,
       or_24_out, rd_diag, ru_diag, tic, zero_or_not_1_out_2, zero_or_not_2_out_2, zero_or_not_3_out_2,
       zero_or_not_4_out_2, zero_or_not_5_out_2, zero_or_not_6_out_2, zero_or_not_7_out_2,
       zero_or_not_8_out_2, zero_or_not_9_out_2, zero_or_not_10_out_2, zero_or_not_11_out_2,
       zero_or_not_12_out_2, zero_or_not_14_out_2, zero_or_not_15_out_2, zero_or_not_16_out_2,
       zero_or_not_17_out_2, zero_or_not_18_out_2;
  wire [5:0] after_ver_paint_b_1, after_ver_paint_b_2, after_ver_paint_b_3, after_ver_paint_b_4,
       after_ver_paint_b_5, after_ver_paint_b_6, after_ver_paint_w_1, after_ver_paint_w_2,
       after_ver_paint_w_3, after_ver_paint_w_4, after_ver_paint_w_5, after_ver_paint_w_6, and_1_out,
       and_4_out, and_7_out, and_12_out, and_15_out, and_18_out, and_21_out, and_23_out, black1_diag,
       black2_diag, black3_diag, black4_diag, black5_diag, black6_diag, black_col, coloring_black_hor,
       coloring_black_ver, coloring_white_hor, coloring_white_ver, do_res, down_ver1, down_ver2, down_ver3,
       down_ver4, down_ver5, down_ver6, ld_max, left_hor1, left_hor2, left_hor3, left_hor4, left_hor5,
       left_hor6, lu_max, now_row, or_1_out, or_2_out, or_3_out, or_4_out, or_5_out, or_6_out, or_13_out,
       or_14_out, or_15_out, or_17_out, or_18_out, or_19_out, or_20_out, or_21_out, or_22_out, or_25_out,
       out_b_1, out_b_2, out_b_3, out_b_4, out_b_5, out_b_6, out_w_1, out_w_2, out_w_4, out_w_5,
       pull_resistor_2_node, pull_resistor_4_node, pull_resistor_5_node, pull_resistor_6_node,
       pull_resistor_7_node, pull_resistor_8_node, pull_resistor_10_node, pull_resistor_11_node,
       pull_resistor_17_node, pull_resistor_18_node, pull_resistor_22_node, pull_resistor_26_node,
       pull_resistor_27_node, pull_resistor_29_node, pull_resistor_31_node, pull_resistor_32_node,
       pull_resistor_33_node, pull_resistor_34_node, pull_resistor_35_node, pull_resistor_36_node,
       pull_resistor_37_node, pull_resistor_39_node, pull_resistor_40_node, pull_resistor_41_node,
       pull_resistor_45_node, pull_resistor_47_node, pull_resistor_50_node, rd_max, right_hor1, right_hor2,
       right_hor3, right_hor4, right_hor5, right_hor6, ru_max, transistor_3_out, transistor_9_out,
       transistor_12_out, transistor_13_out, transistor_14_out, transistor_15_out, transistor_16_out,
       transistor_19_out, transistor_20_out, transistor_21_out, transistor_23_out, transistor_24_out,
       transistor_25_out, transistor_28_out, transistor_30_out, transistor_38_out, transistor_42_out,
       transistor_43_out, transistor_44_out, transistor_46_out, transistor_47_out, transistor_48_out,
       transistor_49_out, transistor_51_out, transistor_53_out, up_ver1, up_ver2, up_ver3, up_ver4, up_ver5,
       up_ver6, white1, white1_diag, white2, white2_diag, white3, white3_diag, white4, white4_diag, white5,
       white5_diag, white6, white6_diag, white_col;

  Clock clock_1 (.out(tic));
  Demultiplexer #(.select(3)) demultiplexer_1 (
    .out0(_1), .out1(_2), .out2(_3), .out3(_4), .out4(_5), .out5(_6), .in(1'b1), .sel(in_5));  // open: out6, out7, en
  Transistor #(.\type ("n"), .gate("br"), .width(6)) transistor_1 (.in({6{1'b0}}), .out(do_res), .gate(in_3));
  Pull_Resistor #(.pull(1)) pull_resistor_1 (.node(do_res));
  can_put can_put_1 (
    .in_1(in_4), .in_2(white1), .in_3(out_6), .in_11(in_1), .in_12(in_2), .in_13(_1), .out_15(can_w1),
    .in_4(black_col), .in_5(white_col), .in_8(now_row), .in_14(in_3), .in_6(lu_diag), .in_7(ru_diag),
    .in_9(ld_diag), .in_10(rd_diag), .left_hor(left_hor1), .rigth_hor(right_hor1), .down_ver(down_ver1),
    .up_ver(up_ver1));
  can_put can_put_2 (
    .in_1(in_4), .in_2(white2), .in_3(out_8), .in_11(in_1), .in_12(in_2), .in_13(_2), .out_15(can_w2),
    .in_4(black_col), .in_5(white_col), .in_8(now_row), .in_14(in_3), .in_6(lu_diag), .in_7(ru_diag),
    .in_9(ld_diag), .in_10(rd_diag), .left_hor(left_hor2), .rigth_hor(right_hor2), .down_ver(down_ver2),
    .up_ver(up_ver2));
  Pull_Resistor pull_resistor_2 (.node(pull_resistor_2_node));
  Transistor #(.\type ("n"), .width(6)) transistor_2 (
    .in(coloring_white_hor), .out(pull_resistor_2_node), .gate(can_w4));
  Transistor #(.\type ("n"), .width(6)) transistor_3 (.in(in_4), .out(transistor_3_out), .gate(can_w4));
  Pull_Resistor pull_resistor_3 (.node(transistor_3_out));
  Pull_Resistor pull_resistor_4 (.node(pull_resistor_4_node));
  Transistor #(.\type ("n"), .width(6)) transistor_4 (
    .in(coloring_white_hor), .out(pull_resistor_4_node), .gate(can_w5));
  Pull_Resistor pull_resistor_5 (.node(pull_resistor_5_node));
  Transistor #(.\type ("n"), .width(6)) transistor_5 (.in(in_4), .out(pull_resistor_5_node), .gate(can_w5));
  Pull_Resistor pull_resistor_6 (.node(pull_resistor_6_node));
  Transistor #(.\type ("n"), .width(6)) transistor_6 (.in(in_4), .out(pull_resistor_6_node), .gate(can_w1));
  Pull_Resistor pull_resistor_7 (.node(pull_resistor_7_node));
  Transistor #(.\type ("n"), .width(6)) transistor_7 (.in(6'b001000), .out(pull_resistor_7_node), .gate(in_1));
  Pull_Resistor pull_resistor_8 (.node(pull_resistor_8_node));
  Transistor #(.\type ("n"), .width(6)) transistor_8 (.in(in_4), .out(pull_resistor_8_node), .gate(can_w3));
  Transistor #(.\type ("n"), .width(6)) transistor_9 (.in(coloring_white_hor), .out(transistor_9_out), .gate(can_w3));
  Pull_Resistor pull_resistor_9 (.node(transistor_9_out));
  Pull_Resistor pull_resistor_10 (.node(pull_resistor_10_node));
  Transistor #(.\type ("n"), .width(6)) transistor_10 (.in(6'b001000), .out(pull_resistor_10_node), .gate(in_1));
  assign or_1_out = white4 | pull_resistor_10_node | white4_diag | pull_resistor_2_node | transistor_3_out | after_ver_paint_w_4;  // OR_Gate or_1, 6 bits wide
  assign or_2_out = white5 | pull_resistor_4_node | white5_diag | after_ver_paint_w_5 | pull_resistor_5_node;  // OR_Gate or_2, 6 bits wide
  Pull_Resistor pull_resistor_11 (.node(pull_resistor_11_node));
  Transistor #(.\type ("n"), .width(6)) transistor_11 (
    .in(coloring_white_hor), .out(pull_resistor_11_node), .gate(can_w6));
  Transistor #(.\type ("n"), .width(6)) transistor_12 (.in(in_4), .out(transistor_12_out), .gate(can_w6));
  Pull_Resistor pull_resistor_12 (.node(transistor_12_out));
  can_put can_put_3 (
    .in_1(in_4), .in_2(white3), .in_3(out_10), .in_11(in_1), .in_12(in_2), .in_13(_3), .out_15(can_w3),
    .in_4(black_col), .in_5(white_col), .in_8(now_row), .in_14(in_3), .in_6(lu_diag), .in_7(ru_diag),
    .in_9(ld_diag), .in_10(rd_diag), .left_hor(left_hor3), .rigth_hor(right_hor3), .down_ver(down_ver3),
    .up_ver(up_ver3));
  can_put can_put_4 (
    .in_1(in_4), .in_2(white4), .in_3(out_12), .in_11(in_1), .in_12(in_2), .in_13(_4), .out_15(can_w4),
    .in_4(black_col), .in_5(white_col), .in_8(now_row), .in_14(in_3), .in_6(lu_diag), .in_7(ru_diag),
    .in_9(ld_diag), .in_10(rd_diag), .left_hor(left_hor4), .rigth_hor(right_hor4), .down_ver(down_ver4),
    .up_ver(up_ver4));
  check_diag_lu check_diag_lu_1 (
    .in_1(white1), .in_2(out_6), .in_3(white2), .in_4(out_8), .in_5(white3), .in_6(out_10), .in_7(white4),
    .in_8(out_12), .in_9(white5), .in_10(out_14), .in_11(white6), .in_12(out_17), .column(in_4),
    .row(now_row), .out_15(lu_diag), .out_col(lu_max));
  check_diag_ld check_diag_ld_1 (
    .in_1(white1), .in_2(out_6), .in_3(white2), .in_4(out_8), .in_5(white3), .in_6(out_10), .in_7(white4),
    .in_8(out_12), .in_9(white5), .in_10(out_14), .in_11(white6), .in_12(out_17), .column(in_4),
    .row(now_row), .out_15(ld_diag), .out_col(ld_max));
  Transistor #(.\type ("n"), .width(6)) transistor_13 (.in(coloring_white_hor), .out(transistor_13_out), .gate(can_w1));
  Pull_Resistor pull_resistor_13 (.node(transistor_13_out));
  Transistor #(.\type ("n"), .width(6)) transistor_14 (.in(coloring_white_hor), .out(transistor_14_out), .gate(can_w2));
  Pull_Resistor pull_resistor_14 (.node(transistor_14_out));
  Transistor #(.\type ("n"), .width(6)) transistor_15 (.in(in_4), .out(transistor_15_out), .gate(can_w2));
  Pull_Resistor pull_resistor_15 (.node(transistor_15_out));
  assign or_3_out = white3 | pull_resistor_7_node | after_ver_paint_w_3 | white3_diag | pull_resistor_8_node | transistor_9_out;  // OR_Gate or_3, 6 bits wide
  zero_or_not zero_or_not_1 (.in_1(after_ver_paint_w_4), .out_2(zero_or_not_1_out_2));
  Transistor #(.\type ("n"), .width(6)) transistor_16 (.in(out_w_5), .out(transistor_16_out), .gate(bot_move));
  Pull_Resistor #(.pull(1)) pull_resistor_16 (.node(transistor_16_out));
  zero_or_not zero_or_not_2 (.in_1(white5_diag), .out_2(zero_or_not_2_out_2));
  zero_or_not zero_or_not_3 (.in_1(after_ver_paint_w_5), .out_2(zero_or_not_3_out_2));
  assign or_4_out = white6 | pull_resistor_11_node | white6_diag | after_ver_paint_w_6 | transistor_12_out;  // OR_Gate or_4, 6 bits wide
  can_put can_put_5 (
    .in_1(in_4), .in_2(white5), .in_3(out_14), .in_11(in_1), .in_12(in_2), .in_13(_5), .out_15(can_w5),
    .in_4(black_col), .in_5(white_col), .in_8(now_row), .in_14(in_3), .in_6(lu_diag), .in_7(ru_diag),
    .in_9(ld_diag), .in_10(rd_diag), .left_hor(left_hor5), .rigth_hor(right_hor5), .down_ver(down_ver5),
    .up_ver(up_ver5));
  can_put can_put_6 (
    .in_1(in_4), .in_2(white6), .in_3(out_17), .in_11(in_1), .in_12(in_2), .in_13(_6), .out_15(can_w6),
    .in_4(black_col), .in_5(white_col), .in_8(now_row), .in_14(in_3), .in_6(lu_diag), .in_7(ru_diag),
    .in_9(ld_diag), .in_10(rd_diag), .left_hor(left_hor6), .rigth_hor(right_hor6), .down_ver(down_ver6),
    .up_ver(up_ver6));
  assign or_5_out = white1 | transistor_13_out | white1_diag | after_ver_paint_w_1 | pull_resistor_6_node;  // OR_Gate or_5, 6 bits wide
  assign or_6_out = white2 | transistor_14_out | white2_diag | after_ver_paint_w_2 | transistor_15_out;  // OR_Gate or_6, 6 bits wide
  zero_or_not zero_or_not_4 (.in_1(white2_diag), .out_2(zero_or_not_4_out_2));
  Pull_Resistor #(.pull(1)) pull_resistor_17 (.node(pull_resistor_17_node));
  Transistor #(.\type ("n"), .width(6)) transistor_17 (.in(out_w_2), .out(pull_resistor_17_node), .gate(bot_move));
  zero_or_not zero_or_not_5 (.in_1(white3_diag), .out_2(zero_or_not_5_out_2));
  zero_or_not zero_or_not_6 (.in_1(after_ver_paint_w_3), .out_2(zero_or_not_6_out_2));
  assign and_1_out = or_1_out & pull_resistor_18_node & do_res;  // AND_Gate and_1, 6 bits wide
  Pull_Resistor #(.pull(1)) pull_resistor_18 (.node(pull_resistor_18_node));
  Transistor #(.\type ("n"), .width(6)) transistor_18 (.in(out_w_4), .out(pull_resistor_18_node), .gate(bot_move));
  zero_or_not zero_or_not_7 (.in_1(white4_diag), .out_2(zero_or_not_7_out_2));
  or or_7 (or_7_out, can_w4, and_2_out, and_3_out);
  and and_2 (and_2_out, zero_or_not_7_out_2, out_15);
  and and_3 (and_3_out, zero_or_not_1_out_2, out_15);
  assign and_4_out = or_2_out & transistor_16_out & do_res;  // AND_Gate and_4, 6 bits wide
  or or_8 (or_8_out, can_w5, and_5_out, and_6_out);
  and and_5 (and_5_out, zero_or_not_2_out_2, out_15);
  and and_6 (and_6_out, zero_or_not_3_out_2, out_15);
  assign and_7_out = or_4_out & transistor_19_out & do_res;  // AND_Gate and_7, 6 bits wide
  Transistor #(.\type ("n"), .width(6)) transistor_19 (.in(out_w_5), .out(transistor_19_out), .gate(bot_move));
  Pull_Resistor #(.pull(1)) pull_resistor_19 (.node(transistor_19_out));
  zero_or_not zero_or_not_8 (.in_1(white6_diag), .out_2(zero_or_not_8_out_2));
  and and_8 (and_8_out, zero_or_not_8_out_2, out_15);
  or or_9 (or_9_out, can_w6, and_8_out, and_9_out);
  zero_or_not zero_or_not_9 (.in_1(after_ver_paint_w_6), .out_2(zero_or_not_9_out_2));
  and and_9 (and_9_out, zero_or_not_9_out_2, out_15);
  check_diag_ru check_diag_ru_1 (
    .in_1(white1), .in_2(out_6), .in_3(white2), .in_4(out_8), .in_5(white3), .in_6(out_10), .in_7(white4),
    .in_8(out_12), .in_9(white5), .in_10(out_14), .in_11(white6), .in_12(out_17), .column(in_4),
    .row(now_row), .out_15(ru_diag), .out_col(ru_max));
  check_diag_rd check_diag_rd_1 (
    .in_1(white1), .in_2(out_6), .in_3(white2), .in_4(out_8), .in_5(white3), .in_6(out_10), .in_7(white4),
    .in_8(out_12), .in_9(white5), .in_10(out_14), .in_11(white6), .in_12(out_17), .column(in_4),
    .row(now_row), .out_15(rd_diag), .out_col(rd_max));
  Transistor #(.\type ("n"), .width(6)) transistor_20 (.in(out_w_1), .out(transistor_20_out), .gate(bot_move));
  Pull_Resistor #(.pull(1)) pull_resistor_20 (.node(transistor_20_out));
  zero_or_not zero_or_not_10 (.in_1(white1_diag), .out_2(zero_or_not_10_out_2));
  and and_10 (and_10_out, zero_or_not_10_out_2, out_15);
  zero_or_not zero_or_not_11 (.in_1(after_ver_paint_w_1), .out_2(zero_or_not_11_out_2));
  and and_11 (and_11_out, zero_or_not_11_out_2, out_15);
  assign and_12_out = or_6_out & transistor_21_out & do_res;  // AND_Gate and_12, 6 bits wide
  Transistor #(.\type ("n"), .width(6)) transistor_21 (.in(out_w_2), .out(transistor_21_out), .gate(bot_move));
  Pull_Resistor #(.pull(1)) pull_resistor_21 (.node(transistor_21_out));
  and and_13 (and_13_out, zero_or_not_4_out_2, out_15);
  zero_or_not zero_or_not_12 (.in_1(after_ver_paint_w_2), .out_2(zero_or_not_12_out_2));
  and and_14 (and_14_out, zero_or_not_12_out_2, out_15);
  assign and_15_out = or_3_out & pull_resistor_17_node & do_res;  // AND_Gate and_15, 6 bits wide
  or or_10 (or_10_out, can_w3, and_16_out, and_17_out);
  and and_16 (and_16_out, zero_or_not_5_out_2, out_15);
  and and_17 (and_17_out, zero_or_not_6_out_2, out_15);
  Register #(.width(6)) register_1 (.D(and_1_out), .en(or_7_out), .Q(white4), .clk(tic));  // open: clr
  Register #(.width(6)) register_2 (.D(and_4_out), .en(or_8_out), .Q(white5), .clk(tic));  // open: clr
  Register #(.width(6)) register_3 (.D(and_7_out), .en(or_9_out), .Q(white6), .clk(tic));  // open: clr
  assign and_18_out = or_5_out & transistor_20_out & do_res;  // AND_Gate and_18, 6 bits wide
  Register #(.width(6)) register_4 (.D(and_18_out), .en(or_11_out), .Q(white1), .clk(tic));  // open: clr
  or or_11 (or_11_out, can_w1, and_10_out, and_11_out);
  Register #(.width(6)) register_5 (.D(and_12_out), .en(or_12_out), .Q(white2), .clk(tic));  // open: clr
  or or_12 (or_12_out, can_w2, and_13_out, and_14_out);
  Register #(.width(6)) register_6 (.D(and_15_out), .en(or_10_out), .Q(white3), .clk(tic));  // open: clr
  assign out_11 = {{1{1'b0}}, white3};  // Bit_Extender bit_extender_1
  assign out_13 = {{1{1'b0}}, white4};  // Bit_Extender bit_extender_2
  assign out_16 = {{1{1'b0}}, white5};  // Bit_Extender bit_extender_3
  assign out_18 = {{1{1'b0}}, white6};  // Bit_Extender bit_extender_4
  column_to_row column_to_row_1 (
    .in_1(in_4), .in_2(out_6), .in_3(out_8), .in_4(out_10), .in_5(out_12), .in_6(out_14), .in_7(out_17),
    .out_8(black_col));
  column_to_row column_to_row_2 (
    .in_1(in_4), .in_2(white1), .in_3(white2), .in_4(white3), .in_5(white4), .in_6(white5), .in_7(white6),
    .out_8(white_col));
  BitAdder #(.width(6)) bitadder_1 (
    .in0(white1), .in1(white2), .in2(white3), .in3(white4), .in4(white5), .in5(white6), .out(white_count));
  BitAdder #(.width(6)) bitadder_2 (
    .in0(out_6), .in1(out_8), .in2(out_10), .in3(out_12), .in4(out_14), .in5(out_17), .out(black_count));
  game_over game_over_1 (
    .in_1(white_count), .in_2(black_count), .white_win(out_21), .draw(out_22), .black_win(out_23),
    .game_over(out_24));
  assign out_7 = {{1{1'b0}}, white1};  // Bit_Extender bit_extender_5
  assign out_9 = {{1{1'b0}}, white2};  // Bit_Extender bit_extender_6
  Multiplexer #(.select(3), .width(6)) multiplexer_1 (
    .in0(6'b000001), .in1(6'b000010), .in2(6'b000100), .in3(6'b001000), .in4(6'b010000), .in5(6'b100000),
    .in7({6{1'b0}}), .out(now_row), .sel(in_5));  // open: in6, en
  Pull_Resistor pull_resistor_22 (.node(pull_resistor_22_node));
  Transistor #(.\type ("n"), .gate("br"), .width(6)) transistor_22 (
    .in(left_hor1), .out(pull_resistor_22_node), .gate(_1));
  Transistor #(.\type ("n"), .gate("br"), .width(6)) transistor_23 (.in(left_hor2), .out(transistor_23_out), .gate(_2));
  Pull_Resistor pull_resistor_23 (.node(transistor_23_out));
  Transistor #(.\type ("n"), .gate("br"), .width(6)) transistor_24 (.in(left_hor3), .out(transistor_24_out), .gate(_3));
  Pull_Resistor pull_resistor_24 (.node(transistor_24_out));
  Transistor #(.\type ("n"), .gate("br"), .width(6)) transistor_25 (
    .in(right_hor1), .out(transistor_25_out), .gate(_1));
  Pull_Resistor pull_resistor_25 (.node(transistor_25_out));
  Pull_Resistor pull_resistor_26 (.node(pull_resistor_26_node));
  Transistor #(.\type ("n"), .gate("br"), .width(6)) transistor_26 (
    .in(right_hor2), .out(pull_resistor_26_node), .gate(_2));
  Pull_Resistor pull_resistor_27 (.node(pull_resistor_27_node));
  Transistor #(.\type ("n"), .gate("br"), .width(6)) transistor_27 (
    .in(right_hor3), .out(pull_resistor_27_node), .gate(_3));
  coloring_diag coloring_diag_1 (
    .max_column_ru(ru_max), .in_2(white1), .in_3(out_6), .in_4(white2), .in_5(out_8), .max_column_lu(lu_max),
    .in_7(white3), .in_8(out_10), .in_9(white4), .in_10(out_12), .max_column_rd(rd_max), .in_12(white5),
    .in_13(out_14), .in_14(white6), .in_15(out_17), .max_column_ld(ld_max), .now_column(in_4),
    .now_row(now_row), .out_19(white1_diag), .out_20(black1_diag), .out_21(white2_diag),
    .out_22(black2_diag), .out_23(white3_diag), .out_24(black3_diag), .out_25(white4_diag),
    .out_26(black4_diag), .out_27(white5_diag), .out_28(black5_diag), .out_29(white6_diag),
    .out_30(black6_diag));
  assign or_13_out = left_hor3 | right_hor3;  // OR_Gate or_13, 6 bits wide
  // Probe on black3_diag
  Transistor #(.\type ("n"), .gate("br"), .width(6)) transistor_28 (.in(left_hor4), .out(transistor_28_out), .gate(_4));
  Pull_Resistor pull_resistor_28 (.node(transistor_28_out));
  Pull_Resistor pull_resistor_29 (.node(pull_resistor_29_node));
  Transistor #(.\type ("n"), .gate("br"), .width(6)) transistor_29 (
    .in(left_hor5), .out(pull_resistor_29_node), .gate(_5));
  Transistor #(.\type ("n"), .gate("br"), .width(6)) transistor_30 (.in(left_hor6), .out(transistor_30_out), .gate(_6));
  Pull_Resistor pull_resistor_30 (.node(transistor_30_out));
  Pull_Resistor pull_resistor_31 (.node(pull_resistor_31_node));
  Transistor #(.\type ("n"), .gate("br"), .width(6)) transistor_31 (
    .in(right_hor4), .out(pull_resistor_31_node), .gate(_4));
  Pull_Resistor pull_resistor_32 (.node(pull_resistor_32_node));
  Transistor #(.\type ("n"), .gate("br"), .width(6)) transistor_32 (
    .in(right_hor5), .out(pull_resistor_32_node), .gate(_5));
  Pull_Resistor pull_resistor_33 (.node(pull_resistor_33_node));
  Transistor #(.\type ("n"), .gate("br"), .width(6)) transistor_33 (
    .in(right_hor6), .out(pull_resistor_33_node), .gate(_6));
  Pull_Resistor pull_resistor_34 (.node(pull_resistor_34_node));
  Transistor #(.\type ("n"), .width(6)) transistor_34 (.in(white1), .out(pull_resistor_34_node), .gate(_1));
  Pull_Resistor pull_resistor_35 (.node(pull_resistor_35_node));
  Transistor #(.\type ("n"), .gate("br"), .width(6)) transistor_35 (.in(out_6), .out(pull_resistor_35_node), .gate(_1));
  Pull_Resistor pull_resistor_36 (.node(pull_resistor_36_node));
  Transistor #(.\type ("n"), .width(6)) transistor_36 (.in(white2), .out(pull_resistor_36_node), .gate(_2));
  Pull_Resistor pull_resistor_37 (.node(pull_resistor_37_node));
  Transistor #(.\type ("n"), .gate("br"), .width(6)) transistor_37 (.in(out_8), .out(pull_resistor_37_node), .gate(_2));
  Transistor #(.\type ("n"), .width(6)) transistor_38 (.in(white3), .out(transistor_38_out), .gate(_3));
  Pull_Resistor pull_resistor_38 (.node(transistor_38_out));
  Pull_Resistor pull_resistor_39 (.node(pull_resistor_39_node));
  Transistor #(.\type ("n"), .gate("br"), .width(6)) transistor_39 (
    .in(out_10), .out(pull_resistor_39_node), .gate(_3));
  Pull_Resistor pull_resistor_40 (.node(pull_resistor_40_node));
  Transistor #(.\type ("n"), .width(6)) transistor_40 (.in(white4), .out(pull_resistor_40_node), .gate(_4));
  Pull_Resistor pull_resistor_41 (.node(pull_resistor_41_node));
  Transistor #(.\type ("n"), .gate("br"), .width(6)) transistor_41 (
    .in(out_12), .out(pull_resistor_41_node), .gate(_4));
  Transistor #(.\type ("n"), .width(6)) transistor_42 (.in(white5), .out(transistor_42_out), .gate(_5));
  Pull_Resistor pull_resistor_42 (.node(transistor_42_out));
  Transistor #(.\type ("n"), .gate("br"), .width(6)) transistor_43 (.in(out_14), .out(transistor_43_out), .gate(_5));
  Pull_Resistor pull_resistor_43 (.node(transistor_43_out));
  Transistor #(.\type ("n"), .width(6)) transistor_44 (.in(white6), .out(transistor_44_out), .gate(_6));
  Pull_Resistor pull_resistor_44 (.node(transistor_44_out));
  Pull_Resistor pull_resistor_45 (.node(pull_resistor_45_node));
  Transistor #(.\type ("n"), .gate("br"), .width(6)) transistor_45 (
    .in(out_17), .out(pull_resistor_45_node), .gate(_6));
  zero_or_not zero_or_not_13 (.in_1(or_14_out), .out_2(bot_move));
  assign or_14_out = out_w_1 | out_w_2 | out_w_2 | out_w_4 | out_w_5 | out_w_5;  // OR_Gate or_14, 6 bits wide
  not not_1 (not_1_out, in_1);
  zero_or_not zero_or_not_14 (.in_1(or_13_out), .out_2(zero_or_not_14_out_2));
  and and_19 (and_19_out, can_w3, zero_or_not_14_out_2, not_1_out);
  Transistor #(.\type ("n"), .width(6)) transistor_46 (
    .in(coloring_black_hor), .out(transistor_46_out), .gate(and_19_out));
  Transistor #(.\type ("n"), .width(6)) transistor_47 (
    .in(black3_diag), .out(transistor_47_out), .gate(do_diag_coloring_3));
  assign or_15_out = left_hor4 | right_hor4;  // OR_Gate or_15, 6 bits wide
  zero_or_not zero_or_not_15 (.in_1(or_15_out), .out_2(zero_or_not_15_out_2));
  not not_2 (not_2_out, in_1);
  and and_20 (and_20_out, can_w4, zero_or_not_15_out_2, not_2_out);
  Transistor #(.\type ("n"), .width(6)) transistor_48 (
    .in(coloring_black_hor), .out(transistor_48_out), .gate(and_20_out));
  Transistor #(.\type ("n"), .width(6)) transistor_49 (
    .in(black4_diag), .out(transistor_49_out), .gate(do_diag_coloring_4));
  Pull_Resistor #(.pull(1)) pull_resistor_46 (.node(transistor_49_out));
  or or_16 (out_15, can_w1, can_w2, can_w3, can_w4, can_w5, can_w6);
  assign or_17_out = pull_resistor_22_node | transistor_23_out | transistor_24_out | transistor_28_out | pull_resistor_29_node | transistor_30_out;  // OR_Gate or_17, 6 bits wide
  assign or_18_out = transistor_25_out | pull_resistor_26_node | pull_resistor_27_node | pull_resistor_31_node | pull_resistor_32_node | pull_resistor_33_node;  // OR_Gate or_18, 6 bits wide
  Pull_Resistor pull_resistor_47 (.node(pull_resistor_47_node));
  Transistor #(.\type ("n"), .width(6)) transistor_50 (.in(in_4), .out(pull_resistor_47_node), .gate(out_15));
  Transistor #(.\type ("n"), .width(6)) transistor_51 (.in(6'b000100), .out(transistor_51_out), .gate(in_1));
  Pull_Resistor pull_resistor_48 (.node(transistor_51_out));
  Pull_Resistor #(.pull(1)) pull_resistor_49 (.node(transistor_47_out));
  Pull_Resistor pull_resistor_50 (.node(pull_resistor_50_node));
  Transistor #(.\type ("n"), .width(6)) transistor_52 (.in(6'b000100), .out(pull_resistor_50_node), .gate(in_1));
  assign or_19_out = pull_resistor_34_node | pull_resistor_36_node | transistor_38_out | pull_resistor_40_node | transistor_42_out | transistor_44_out;  // OR_Gate or_19, 6 bits wide
  assign or_20_out = pull_resistor_35_node | pull_resistor_37_node | pull_resistor_39_node | pull_resistor_41_node | transistor_43_out | pull_resistor_45_node;  // OR_Gate or_20, 6 bits wide
  assign or_21_out = out_10 | transistor_51_out;  // OR_Gate or_21, 6 bits wide
  Pull_Resistor #(.pull(1)) pull_resistor_51 (.node(transistor_46_out));
  assign or_22_out = out_12 | pull_resistor_50_node;  // OR_Gate or_22, 6 bits wide
  Pull_Resistor #(.pull(1)) pull_resistor_52 (.node(transistor_48_out));
  zero_or_not zero_or_not_16 (.in_1(after_ver_paint_w_4), .out_2(zero_or_not_16_out_2));
  Register #(.width(6)) register_7 (.en(1'b1), .Q(out_6), .clk(tic));  // open: D, clr
  Register #(.width(6)) register_8 (.en(1'b1), .Q(out_8), .clk(tic));  // open: D, clr
  assign and_21_out = or_21_out & transistor_46_out & transistor_47_out & do_res & after_ver_paint_b_3;  // AND_Gate and_21, 6 bits wide
  zero_or_not zero_or_not_17 (.in_1(after_ver_paint_w_3), .out_2(zero_or_not_17_out_2));
  and and_22 (and_22_out, zero_or_not_17_out_2, out_15);
  assign and_23_out = or_22_out & transistor_48_out & transistor_49_out & do_res & after_ver_paint_b_4;  // AND_Gate and_23, 6 bits wide
  or or_23 (or_23_out, in_1, can_w4, do_diag_coloring_4, in_3, and_24_out);
  and and_24 (and_24_out, zero_or_not_16_out_2, out_15);
  coloring_hor coloring_hor_1 (
    .min_left(or_17_out), .max_right(or_18_out), .column(pull_resistor_47_node), .now_white(or_19_out),
    .now_black(or_20_out), .out_6(coloring_white_hor), .out_7(coloring_black_hor));
  Register #(.width(6)) register_9 (.D(and_21_out), .en(or_24_out), .Q(out_10), .clk(tic));  // open: clr
  or or_24 (or_24_out, in_1, can_w3, do_diag_coloring_3, in_3, and_22_out);
  Register #(.width(6)) register_10 (.D(and_23_out), .en(or_23_out), .Q(out_12), .clk(tic));  // open: clr
  Register #(.width(6)) register_11 (.en(1'b1), .Q(out_14), .clk(tic));  // open: D, clr
  Register #(.width(6)) register_12 (.en(1'b1), .Q(out_17), .clk(tic));  // open: D, clr
  compare_6bit compare_6bit_1 (.in_1(out_10), .in_2(black3_diag), .out_3(compare_6bit_1_out_3));
  assign or_25_out = up_ver1 | down_ver2;  // OR_Gate or_25, 6 bits wide
  zero_or_not zero_or_not_18 (.in_1(or_25_out), .out_2(zero_or_not_18_out_2));
  Transistor #(.\type ("n"), .width(6)) transistor_53 (
    .in(now_row), .out(transistor_53_out), .gate(zero_or_not_18_out_2));
  Pull_Resistor pull_resistor_53 (.node(transistor_53_out));
  not not_3 (not_3_out, in_1);
  and and_25 (do_diag_coloring_3, out_15, compare_6bit_1_out_3, not_3_out);
  not not_4 (not_4_out, in_1);
  compare_6bit compare_6bit_2 (.in_1(out_12), .in_2(black4_diag), .out_3(compare_6bit_2_out_3));
  and and_26 (do_diag_coloring_4, out_15, compare_6bit_2_out_3, not_4_out);
  row_to_column_for_white row_to_column_for_white_1 (
    .column_white(coloring_white_ver), .column_num(in_4), .out_3(after_ver_paint_w_1),
    .out_4(after_ver_paint_w_2), .out_5(after_ver_paint_w_3), .out_6(after_ver_paint_w_4),
    .out_7(after_ver_paint_w_5), .out_8(after_ver_paint_w_6));
  row_to_column_for_black row_to_column_for_black_1 (
    .column_black(coloring_black_ver), .column_num(in_4), .out_3(after_ver_paint_b_1),
    .out_4(after_ver_paint_b_2), .out_5(after_ver_paint_b_3), .out_6(after_ver_paint_b_4),
    .out_7(after_ver_paint_b_5), .out_8(after_ver_paint_b_6));
  coloring_hor coloring_hor_2 (
    .min_left(down_ver2), .max_right(up_ver1), .column(transistor_53_out), .now_white(white_col),
    .now_black(black_col), .out_6(coloring_white_ver), .out_7(coloring_black_ver));
  wrtr wrtr_1 (
    .white1(white1), .black1(out_6), .white2(white2), .black2(out_8), .white3(white3), .black3(out_10),
    .white4(white4), .black4(out_12), .white5(white5), .black5(out_14), .white6(white6), .black6(out_17),
    .white_out_1(out_w_1), .white_out_2(out_w_2), .white_out_3(out_w_2), .white_out_4(out_w_4),
    .white_out_5(out_w_5), .white_out_6(out_w_5), .black_out_1(out_b_1), .black_out_2(out_b_2),
    .black_out_3(out_b_3), .black_out_4(out_b_4), .black_out_5(out_b_5), .black_out_6(out_b_6));  // open: go, flag_bot_finish

  // Other names for the same wires on the sheet: black1[5:0] = out_6; black2[5:0] = out_8; black3[5:0] = out_10;
  //   black4[5:0] = out_12; black5[5:0] = out_14; black6[5:0] = out_17; can_put = out_15; column[5:0] = in_4;
  //   count_b[5:0] = black_count; count_w[5:0] = white_count; out_w_3[5:0] = out_w_2; out_w_6[5:0] = out_w_5;
  //   reset = in_3; row[2:0] = in_5; start = in_1; turn = in_2
endmodule

module buttons_row (
  input  in_1,
  input  in_2,
  input  in_3,
  input  in_4,
  input  in_5,
  input  in_6,
  output [5:0] out_7
);


  assign out_7 = {in_1, in_2, in_3, in_4, in_5, in_6};

  // Other names for the same wires on the sheet: _0 = in_6; _1 = in_5; _2 = in_4; _3 = in_3; _4 = in_2; _5 = in_1
endmodule

module switch_turn (
  input  in_1,
  input  \сама_кнопка ,
  input  in_3,
  output out_4
);

  and and_1 (out_4, in_1, \сама_кнопка );
  // AND_Gate and_2 has open pins: in0=\сама_кнопка , in1=in_3, out=open

  // Notes on the sheet:
  //   текущие значение т тригера
  //   текущие значение т тригера
endmodule

module if_3bit (
  input  [2:0] Input_0,
  input  sel,
  input  [2:0] Input_1,
  output [2:0] Output
);

  wire [2:0] and_1_out, and_2_out;
  wire [2:2] not_1_out;

  not not_1 (not_1_out[2], sel);
  assign and_1_out = Input_0 & {3{not_1_out[2]}};  // AND_Gate and_1, 3 bits wide
  assign and_2_out = {3{sel}} & Input_1;  // AND_Gate and_2, 3 bits wide
  assign Output = and_1_out | and_2_out;  // OR_Gate or_1, 3 bits wide
endmodule

module if_6bit (
  input  [5:0] Input_0,
  input  sel,
  input  [5:0] Input_1,
  output [5:0] Output
);

  wire [5:0] and_1_out, and_2_out;
  wire [5:5] not_1_out;

  not not_1 (not_1_out[5], sel);
  assign and_1_out = Input_0 & {6{not_1_out[5]}};  // AND_Gate and_1, 6 bits wide
  assign and_2_out = {6{sel}} & Input_1;  // AND_Gate and_2, 6 bits wide
  assign Output = and_1_out | and_2_out;  // OR_Gate or_1, 6 bits wide
endmodule

module compare_6bit (
  input  [5:0] in_1,
  input  [5:0] in_2,
  output out_3
);

  wire comparator_1_eq;

  not not_1 (out_3, comparator_1_eq);
  Comparator #(.width(6)) comparator_1 (.a(in_1), .b(in_2), .eq(comparator_1_eq));  // open: gt, lt

  // Notes on the sheet:
  //   0 if the inputs are equal
endmodule

module column_to_row (
  input  [5:0] in_1,
  input  [5:0] in_2,
  input  [5:0] in_3,
  input  [5:0] in_4,
  input  [5:0] in_5,
  input  [5:0] in_6,
  input  [5:0] in_7,
  output [5:0] out_8
);

  wire [2:0] column, if_3bit_1_output, if_3bit_2_output, if_3bit_3_output, if_3bit_4_output,
       if_3bit_5_output, if_3bit_6_output;

  Multiplexer #(.select(3)) multiplexer_1 (
    .in0(in_2[0]), .in1(in_2[1]), .in2(in_2[2]), .in3(in_2[3]), .in4(in_2[4]), .in5(in_2[5]), .out(out_8[0]),
    .sel(column));  // open: in6, in7, en
  Multiplexer #(.select(3)) multiplexer_2 (
    .in0(in_3[0]), .in1(in_3[1]), .in2(in_3[2]), .in3(in_3[3]), .in4(in_3[4]), .in5(in_3[5]), .out(out_8[1]),
    .sel(column));  // open: in6, in7, en
  Multiplexer #(.select(3)) multiplexer_3 (
    .in0(in_4[0]), .in1(in_4[1]), .in2(in_4[2]), .in3(in_4[3]), .in4(in_4[4]), .in5(in_4[5]), .out(out_8[2]),
    .sel(column));  // open: in6, in7, en
  Multiplexer #(.select(3)) multiplexer_4 (
    .in0(in_5[0]), .in1(in_5[1]), .in2(in_5[2]), .in3(in_5[3]), .in4(in_5[4]), .in5(in_5[5]), .out(out_8[3]),
    .sel(column));  // open: in6, in7, en
  Multiplexer #(.select(3)) multiplexer_5 (
    .in0(in_6[0]), .in1(in_6[1]), .in2(in_6[2]), .in3(in_6[3]), .in4(in_6[4]), .in5(in_6[5]), .out(out_8[4]),
    .sel(column));  // open: in6, in7, en
  Multiplexer #(.select(3)) multiplexer_6 (
    .in0(in_7[0]), .in1(in_7[1]), .in2(in_7[2]), .in3(in_7[3]), .in4(in_7[4]), .in5(in_7[5]), .out(out_8[5]),
    .sel(column));  // open: in6, in7, en
  if_3bit if_3bit_1 (.Input_0(3'b000), .sel(in_1[0]), .Input_1(3'b000), .Output(if_3bit_1_output));
  if_3bit if_3bit_2 (.Input_0(3'b000), .sel(in_1[1]), .Input_1(3'b001), .Output(if_3bit_2_output));
  if_3bit if_3bit_3 (.Input_0(3'b000), .sel(in_1[2]), .Input_1(3'b010), .Output(if_3bit_3_output));
  if_3bit if_3bit_4 (.Input_0(3'b000), .sel(in_1[3]), .Input_1(3'b011), .Output(if_3bit_4_output));
  if_3bit if_3bit_5 (.Input_0(3'b000), .sel(in_1[4]), .Input_1(3'b100), .Output(if_3bit_5_output));
  if_3bit if_3bit_6 (.Input_0(3'b000), .sel(in_1[5]), .Input_1(3'b101), .Output(if_3bit_6_output));
  assign column = if_3bit_1_output | if_3bit_2_output | if_3bit_3_output | if_3bit_4_output | if_3bit_5_output | if_3bit_6_output;  // OR_Gate or_1, 3 bits wide
endmodule

module column_selection (
  input  in_1,
  input  in_2,
  input  in_3,
  input  in_4,
  input  in_5,
  input  in_6,
  input  [5:0] in_7,
  output [5:0] out_8
);

  wire or_1_out;

  or or_1 (or_1_out, in_1, in_2, in_3, in_4, in_5, in_6);
  // Probe on {6{1'b0}}
  if_6bit if_6bit_1 (.Input_0({6{1'b0}}), .sel(or_1_out), .Input_1(in_7), .Output(out_8));
  // Probe on in_7
endmodule

module row_selection (
  input  in_1,
  input  in_2,
  input  in_3,
  input  in_4,
  input  in_5,
  input  in_6,
  input  [2:0] in_7,
  output [2:0] out_8
);

  wire or_1_out;

  or or_1 (or_1_out, in_1, in_2, in_3, in_4, in_5, in_6);
  // Probe on 3'b111
  if_3bit if_3bit_1 (.Input_0(3'b111), .sel(or_1_out), .Input_1(in_7), .Output(out_8));
  // Probe on in_7
endmodule

module check_right (
  input  [5:0] corrent,
  input  [5:0] white,
  input  [5:0] black,
  output out_4,
  output [5:0] out_5
);

  wire _1break, _2break, _3break, _4break, _5break, _6break, and_1_out, and_2_out, and_3_out, and_4_out,
       and_6_out, and_7_out, and_10_out, and_13_out, and_16_out, answer, compare_6bit_1_out_3,
       compare_6bit_2_out_3, compare_6bit_3_out_3, compare_6bit_4_out_3, compare_6bit_5_out_3, not_2_out,
       not_3_out, not_4_out, not_5_out, not_6_out, not_7_out, not_8_out, not_9_out, not_10_out, not_11_out,
       not_12_out, not_13_out, not_14_out, not_15_out, not_17_out, or_1_out, zero_or_not_1_out_2,
       zero_or_not_2_out_2, zero_or_not_3_out_2, zero_or_not_4_out_2, zero_or_not_5_out_2,
       zero_or_not_6_out_2, zero_or_not_7_out_2, zero_or_not_8_out_2;
  wire [2:0] bit_extender_1_out, bit_extender_2_out, bit_extender_3_out, bit_extender_4_out,
       bit_extender_5_out;
  wire [5:0] and_5_out, and_8_out, and_9_out, and_11_out, and_12_out, and_14_out, and_15_out, and_17_out,
       and_18_out, col2, col3, col4, col5, col6, or_2_out, shifter_2_out, transistor_1_out, transistor_2_out,
       transistor_3_out, transistor_4_out, transistor_5_out, transistor_7_out;

  compare_6bit compare_6bit_1 (.in_1(6'b000001), .in_2(corrent), .out_3(compare_6bit_1_out_3));
  assign bit_extender_1_out = {{2{1'b0}}, compare_6bit_1_out_3};  // Bit_Extender bit_extender_1
  not not_1 (_1break, compare_6bit_1_out_3);
  not not_2 (not_2_out, _4break);
  Shifter #(.width(6), .shift("lr")) shifter_1 (.in(corrent), .\dist (bit_extender_1_out), .out(col2));
  not not_3 (not_3_out, _2break);
  and and_1 (and_1_out, _3break, not_3_out, not_13_out);
  not not_4 (not_4_out, _3break);
  not not_5 (not_5_out, _2break);
  not not_6 (not_6_out, _1break);
  and and_2 (and_2_out, _4break, not_4_out, not_5_out, not_6_out);
  Transistor #(.\type ("n"), .width(6)) transistor_1 (.in(col4), .out(transistor_1_out), .gate(and_2_out));
  not not_7 (not_7_out, _3break);
  not not_8 (not_8_out, _2break);
  not not_9 (not_9_out, _1break);
  and and_3 (and_3_out, not_2_out, not_7_out, _5break, not_8_out, not_9_out);
  Transistor #(.\type ("n"), .width(6)) transistor_2 (.in(col5), .out(transistor_2_out), .gate(and_3_out));
  not not_10 (not_10_out, _5break);
  not not_11 (not_11_out, _3break);
  not not_12 (not_12_out, _4break);
  and and_4 (and_4_out, _6break, not_10_out, not_12_out, not_11_out, not_14_out, not_15_out);
  Transistor #(.\type ("n"), .width(6)) transistor_3 (.in(col6), .out(transistor_3_out), .gate(and_4_out));
  compare_6bit compare_6bit_2 (.in_1(6'b000001), .in_2(col2), .out_3(compare_6bit_2_out_3));
  assign and_5_out = col2 & black;  // AND_Gate and_5, 6 bits wide
  zero_or_not zero_or_not_1 (.in_1(and_5_out), .out_2(zero_or_not_1_out_2));
  not not_13 (not_13_out, _1break);
  Transistor #(.\type ("n"), .width(6)) transistor_4 (.in(col3), .out(transistor_4_out), .gate(and_1_out));
  not not_14 (not_14_out, _2break);
  not not_15 (not_15_out, _1break);
  and and_6 (and_6_out, compare_6bit_2_out_3, zero_or_not_1_out_2);
  not not_16 (_2break, and_6_out);
  Pull_Resistor pull_resistor_1 (.node(answer));
  not not_17 (not_17_out, _1break);
  and and_7 (and_7_out, _2break, not_17_out);
  Transistor #(.\type ("n"), .width(6)) transistor_5 (.in(col2), .out(transistor_5_out), .gate(and_7_out));
  Shifter #(.width(6), .shift("lr")) shifter_2 (.in(col2), .\dist (bit_extender_2_out), .out(shifter_2_out));
  assign bit_extender_2_out = {{2{1'b0}}, and_6_out};  // Bit_Extender bit_extender_2
  or or_1 (or_1_out, _1break, _2break, _4break, _3break, _5break, _6break);
  Pull_Resistor pull_resistor_2 (.node(out_4));
  Transistor #(.\type ("n")) transistor_6 (.in(answer), .out(out_4), .gate(or_1_out));
  Transistor #(.\type ("n"), .width(6)) transistor_7 (.in(corrent), .out(transistor_7_out), .gate(_1break));
  Pull_Resistor pull_resistor_3 (.node(transistor_2_out));
  Pull_Resistor pull_resistor_4 (.node(col3));
  Transistor #(.width(6)) transistor_8 (.in(shifter_2_out), .out(col3), .gate(_2break));
  Pull_Resistor pull_resistor_5 (.node(transistor_7_out));
  Pull_Resistor pull_resistor_6 (.node(transistor_5_out));
  Pull_Resistor pull_resistor_7 (.node(transistor_4_out));
  Pull_Resistor pull_resistor_8 (.node(transistor_1_out));
  compare_6bit compare_6bit_3 (.in_1(6'b000001), .in_2(col3), .out_3(compare_6bit_3_out_3));
  assign and_8_out = col3 & black;  // AND_Gate and_8, 6 bits wide
  zero_or_not zero_or_not_2 (.in_1(and_8_out), .out_2(zero_or_not_2_out_2));
  zero_or_not zero_or_not_3 (.in_1(and_9_out), .out_2(zero_or_not_3_out_2));
  assign and_9_out = col3 & white;  // AND_Gate and_9, 6 bits wide
  assign or_2_out = transistor_7_out | transistor_5_out | transistor_4_out | transistor_1_out | transistor_2_out | transistor_3_out;  // OR_Gate or_2, 6 bits wide
  Pull_Resistor pull_resistor_9 (.node(transistor_3_out));
  and and_10 (and_10_out, compare_6bit_3_out_3, zero_or_not_2_out_2);
  not not_18 (_3break, and_10_out);
  Transistor transistor_9 (.in(zero_or_not_3_out_2), .out(answer), .gate(zero_or_not_2_out_2));
  Transistor #(.\type ("n"), .width(6)) transistor_10 (.in(or_2_out), .out(out_5), .gate(answer));
  Pull_Resistor pull_resistor_10 (.node(out_5));
  Shifter #(.width(6), .shift("lr")) shifter_3 (.in(col3), .\dist (bit_extender_3_out), .out(col4));
  assign bit_extender_3_out = {{2{1'b0}}, and_10_out};  // Bit_Extender bit_extender_3
  assign and_11_out = col4 & black;  // AND_Gate and_11, 6 bits wide
  zero_or_not zero_or_not_4 (.in_1(and_11_out), .out_2(zero_or_not_4_out_2));
  assign and_12_out = col4 & white;  // AND_Gate and_12, 6 bits wide
  zero_or_not zero_or_not_5 (.in_1(and_12_out), .out_2(zero_or_not_5_out_2));
  compare_6bit compare_6bit_4 (.in_1(6'b000001), .in_2(col4), .out_3(compare_6bit_4_out_3));
  and and_13 (and_13_out, compare_6bit_4_out_3, zero_or_not_4_out_2);
  not not_19 (_4break, and_13_out);
  Transistor transistor_11 (.in(zero_or_not_5_out_2), .out(answer), .gate(zero_or_not_4_out_2));
  assign bit_extender_4_out = {{2{1'b0}}, and_13_out};  // Bit_Extender bit_extender_4
  Shifter #(.width(6), .shift("lr")) shifter_4 (.in(col4), .\dist (bit_extender_4_out), .out(col5));
  assign and_14_out = col5 & black;  // AND_Gate and_14, 6 bits wide
  assign and_15_out = col5 & white;  // AND_Gate and_15, 6 bits wide
  compare_6bit compare_6bit_5 (.in_1(6'b000001), .in_2(col5), .out_3(compare_6bit_5_out_3));
  and and_16 (and_16_out, compare_6bit_5_out_3, zero_or_not_6_out_2);
  zero_or_not zero_or_not_6 (.in_1(and_14_out), .out_2(zero_or_not_6_out_2));
  not not_20 (_5break, and_16_out);
  zero_or_not zero_or_not_7 (.in_1(and_15_out), .out_2(zero_or_not_7_out_2));
  Transistor transistor_12 (.in(zero_or_not_7_out_2), .out(answer), .gate(zero_or_not_6_out_2));
  assign bit_extender_5_out = {{2{1'b0}}, and_16_out};  // Bit_Extender bit_extender_5
  Shifter #(.width(6), .shift("lr")) shifter_5 (.in(col5), .\dist (bit_extender_5_out), .out(col6));
  not not_21 (_6break, zero_or_not_8_out_2);
  zero_or_not zero_or_not_8 (.in_1(and_17_out), .out_2(zero_or_not_8_out_2));
  assign and_17_out = col6 & black;  // AND_Gate and_17, 6 bits wide
  zero_or_not zero_or_not_9 (.in_1(and_18_out), .out_2(answer));
  assign and_18_out = col6 & white;  // AND_Gate and_18, 6 bits wide

  // Other names for the same wires on the sheet: col1[5:0] = corrent
endmodule

module check_left (
  input  [5:0] corrent,
  input  [5:0] white,
  input  [5:0] black,
  output out_4,
  output [5:0] out_5
);

  wire _1break, _2break, _3break, _4break, _5break, _6break, and_1_out, and_2_out, and_3_out, and_4_out,
       and_6_out, and_7_out, and_10_out, and_13_out, and_16_out, answer, compare_6bit_1_out_3,
       compare_6bit_2_out_3, compare_6bit_3_out_3, compare_6bit_4_out_3, compare_6bit_5_out_3, not_2_out,
       not_3_out, not_4_out, not_5_out, not_6_out, not_7_out, not_8_out, not_9_out, not_10_out, not_11_out,
       not_12_out, not_13_out, not_14_out, not_15_out, not_17_out, or_1_out, zero_or_not_1_out_2,
       zero_or_not_2_out_2, zero_or_not_3_out_2, zero_or_not_4_out_2, zero_or_not_5_out_2,
       zero_or_not_6_out_2, zero_or_not_7_out_2, zero_or_not_8_out_2;
  wire [2:0] bit_extender_1_out, bit_extender_2_out, bit_extender_3_out, bit_extender_4_out,
       bit_extender_5_out;
  wire [5:0] and_5_out, and_8_out, and_9_out, and_11_out, and_12_out, and_14_out, and_15_out, and_17_out,
       and_18_out, col2, col3, col4, col5, col6, or_2_out, shifter_2_out, transistor_1_out, transistor_2_out,
       transistor_3_out, transistor_4_out, transistor_5_out, transistor_7_out;

  compare_6bit compare_6bit_1 (.in_1(6'b100000), .in_2(corrent), .out_3(compare_6bit_1_out_3));
  assign bit_extender_1_out = {{2{1'b0}}, compare_6bit_1_out_3};  // Bit_Extender bit_extender_1
  not not_1 (_1break, compare_6bit_1_out_3);
  not not_2 (not_2_out, _4break);
  Shifter #(.width(6)) shifter_1 (.in(corrent), .\dist (bit_extender_1_out), .out(col2));
  not not_3 (not_3_out, _2break);
  and and_1 (and_1_out, _3break, not_3_out, not_13_out);
  not not_4 (not_4_out, _3break);
  not not_5 (not_5_out, _1break);
  not not_6 (not_6_out, _2break);
  and and_2 (and_2_out, _4break, not_4_out, not_6_out, not_5_out);
  Transistor #(.\type ("n"), .width(6)) transistor_1 (.in(col4), .out(transistor_1_out), .gate(and_2_out));
  not not_7 (not_7_out, _2break);
  not not_8 (not_8_out, _3break);
  not not_9 (not_9_out, _1break);
  and and_3 (and_3_out, not_2_out, not_8_out, _5break, not_7_out, not_9_out);
  Transistor #(.\type ("n"), .width(6)) transistor_2 (.in(col5), .out(transistor_2_out), .gate(and_3_out));
  not not_10 (not_10_out, _3break);
  not not_11 (not_11_out, _5break);
  not not_12 (not_12_out, _4break);
  and and_4 (and_4_out, _6break, not_11_out, not_12_out, not_10_out, not_15_out, not_14_out);
  Transistor #(.\type ("n"), .width(6)) transistor_3 (.in(col6), .out(transistor_3_out), .gate(and_4_out));
  compare_6bit compare_6bit_2 (.in_1(6'b100000), .in_2(col2), .out_3(compare_6bit_2_out_3));
  zero_or_not zero_or_not_1 (.in_1(and_5_out), .out_2(zero_or_not_1_out_2));
  assign and_5_out = col2 & black;  // AND_Gate and_5, 6 bits wide
  not not_13 (not_13_out, _1break);
  Transistor #(.\type ("n"), .width(6)) transistor_4 (.in(col3), .out(transistor_4_out), .gate(and_1_out));
  not not_14 (not_14_out, _1break);
  not not_15 (not_15_out, _2break);
  and and_6 (and_6_out, compare_6bit_2_out_3, zero_or_not_1_out_2);
  not not_16 (_2break, and_6_out);
  or or_1 (or_1_out, _1break, _2break, _4break, _3break, _5break, _6break);
  Pull_Resistor pull_resistor_1 (.node(answer));
  not not_17 (not_17_out, _1break);
  and and_7 (and_7_out, _2break, not_17_out);
  Transistor #(.\type ("n"), .width(6)) transistor_5 (.in(col2), .out(transistor_5_out), .gate(and_7_out));
  Shifter #(.width(6)) shifter_2 (.in(col2), .\dist (bit_extender_2_out), .out(shifter_2_out));
  assign bit_extender_2_out = {{2{1'b0}}, and_6_out};  // Bit_Extender bit_extender_2
  Transistor #(.\type ("n")) transistor_6 (.in(answer), .out(out_4), .gate(or_1_out));
  Pull_Resistor pull_resistor_2 (.node(out_4));
  Transistor #(.\type ("n"), .width(6)) transistor_7 (.in(corrent), .out(transistor_7_out), .gate(_1break));
  Pull_Resistor pull_resistor_3 (.node(transistor_2_out));
  Transistor #(.width(6)) transistor_8 (.in(shifter_2_out), .out(col3), .gate(_2break));
  Pull_Resistor pull_resistor_4 (.node(col3));
  Pull_Resistor pull_resistor_5 (.node(transistor_5_out));
  Pull_Resistor pull_resistor_6 (.node(transistor_4_out));
  Pull_Resistor pull_resistor_7 (.node(transistor_1_out));
  compare_6bit compare_6bit_3 (.in_1(6'b100000), .in_2(col3), .out_3(compare_6bit_3_out_3));
  assign and_8_out = col3 & black;  // AND_Gate and_8, 6 bits wide
  zero_or_not zero_or_not_2 (.in_1(and_8_out), .out_2(zero_or_not_2_out_2));
  assign and_9_out = col3 & white;  // AND_Gate and_9, 6 bits wide
  zero_or_not zero_or_not_3 (.in_1(and_9_out), .out_2(zero_or_not_3_out_2));
  Pull_Resistor pull_resistor_8 (.node(transistor_7_out));
  assign or_2_out = transistor_7_out | transistor_5_out | transistor_4_out | transistor_1_out | transistor_2_out | transistor_3_out;  // OR_Gate or_2, 6 bits wide
  Pull_Resistor pull_resistor_9 (.node(transistor_3_out));
  and and_10 (and_10_out, compare_6bit_3_out_3, zero_or_not_2_out_2);
  not not_18 (_3break, and_10_out);
  Transistor transistor_9 (.in(zero_or_not_3_out_2), .out(answer), .gate(zero_or_not_2_out_2));
  Pull_Resistor pull_resistor_10 (.node(out_5));
  Transistor #(.\type ("n"), .width(6)) transistor_10 (.in(or_2_out), .out(out_5), .gate(answer));
  Shifter #(.width(6)) shifter_3 (.in(col3), .\dist (bit_extender_3_out), .out(col4));
  assign bit_extender_3_out = {{2{1'b0}}, and_10_out};  // Bit_Extender bit_extender_3
  assign and_11_out = col4 & black;  // AND_Gate and_11, 6 bits wide
  zero_or_not zero_or_not_4 (.in_1(and_11_out), .out_2(zero_or_not_4_out_2));
  zero_or_not zero_or_not_5 (.in_1(and_12_out), .out_2(zero_or_not_5_out_2));
  assign and_12_out = col4 & white;  // AND_Gate and_12, 6 bits wide
  compare_6bit compare_6bit_4 (.in_1(6'b100000), .in_2(col4), .out_3(compare_6bit_4_out_3));
  and and_13 (and_13_out, compare_6bit_4_out_3, zero_or_not_4_out_2);
  not not_19 (_4break, and_13_out);
  Transistor transistor_11 (.in(zero_or_not_5_out_2), .out(answer), .gate(zero_or_not_4_out_2));
  assign bit_extender_4_out = {{2{1'b0}}, and_13_out};  // Bit_Extender bit_extender_4
  Shifter #(.width(6)) shifter_4 (.in(col4), .\dist (bit_extender_4_out), .out(col5));
  assign and_14_out = col5 & black;  // AND_Gate and_14, 6 bits wide
  assign and_15_out = col5 & white;  // AND_Gate and_15, 6 bits wide
  compare_6bit compare_6bit_5 (.in_1(6'b100000), .in_2(col5), .out_3(compare_6bit_5_out_3));
  and and_16 (and_16_out, compare_6bit_5_out_3, zero_or_not_6_out_2);
  zero_or_not zero_or_not_6 (.in_1(and_14_out), .out_2(zero_or_not_6_out_2));
  not not_20 (_5break, and_16_out);
  Transistor transistor_12 (.in(zero_or_not_7_out_2), .out(answer), .gate(zero_or_not_6_out_2));
  zero_or_not zero_or_not_7 (.in_1(and_15_out), .out_2(zero_or_not_7_out_2));
  assign bit_extender_5_out = {{2{1'b0}}, and_16_out};  // Bit_Extender bit_extender_5
  Shifter #(.width(6)) shifter_5 (.in(col5), .\dist (bit_extender_5_out), .out(col6));
  zero_or_not zero_or_not_8 (.in_1(and_17_out), .out_2(zero_or_not_8_out_2));
  not not_21 (_6break, zero_or_not_8_out_2);
  assign and_17_out = col6 & black;  // AND_Gate and_17, 6 bits wide
  assign and_18_out = col6 & white;  // AND_Gate and_18, 6 bits wide
  zero_or_not zero_or_not_9 (.in_1(and_18_out), .out_2(answer));

  // Other names for the same wires on the sheet: col1[5:0] = corrent
endmodule

module check_diag_ru (
  input  [5:0] in_1,
  input  [5:0] in_2,
  input  [5:0] in_3,
  input  [5:0] in_4,
  input  [5:0] in_5,
  input  [5:0] in_6,
  input  [5:0] in_7,
  input  [5:0] in_8,
  input  [5:0] in_9,
  input  [5:0] in_10,
  input  [5:0] in_11,
  input  [5:0] in_12,
  input  [5:0] column,
  input  [5:0] row,
  output out_15,
  output [5:0] out_col
);

  wire _0break_c, _0break_r, _1break_c, _1break_r, _2break_c, _2break_r, _3break_c, _3break_r, _4break_c,
       _4break_r, _5break_c, _5break_r, and_1_out, and_2_out, and_3_out, and_5_out, and_6_out, and_7_out,
       and_10_out, and_13_out, answer2, answer3, answer4, answer5, compare_6bit_1_out_3,
       compare_6bit_2_out_3, compare_6bit_3_out_3, compare_6bit_4_out_3, compare_6bit_5_out_3,
       compare_6bit_6_out_3, compare_6bit_7_out_3, compare_6bit_8_out_3, compare_6bit_9_out_3,
       compare_6bit_10_out_3, compare_6bit_11_out_3, not_1_out, not_2_out, not_5_out, not_6_out, not_7_out,
       not_8_out, not_9_out, not_10_out, not_12_out, not_13_out, not_15_out, not_16_out, not_17_out,
       not_19_out, or_1_out, or_2_out, or_3_out, or_4_out, or_5_out, or_6_out, or_7_out, or_8_out, or_9_out,
       or_10_out, or_11_out, or_12_out, or_14_out, or_15_out, or_16_out, or_17_out, or_18_out, or_19_out,
       or_20_out, or_21_out, or_22_out, or_23_out, or_24_out, or_26_out, or_27_out, or_28_out,
       pull_resistor_5_node, zero_or_not_1_out_2, zero_or_not_2_out_2, zero_or_not_3_out_2,
       zero_or_not_4_out_2, zero_or_not_5_out_2, zero_or_not_6_out_2, zero_or_not_7_out_2,
       zero_or_not_8_out_2;
  wire [2:0] bit_extender_1_out, bit_extender_2_out, bit_extender_3_out, bit_extender_4_out,
       bit_extender_5_out, bit_extender_6_out, bit_extender_7_out, bit_extender_8_out, bit_extender_9_out,
       bit_extender_10_out, n6numrow_to_3numrow_1_out_2, n6numrow_to_3numrow_2_out_2,
       n6numrow_to_3numrow_3_out_2, n6numrow_to_3numrow_4_out_2, n6numrow_to_3numrow_5_out_2,
       n6numrow_to_3numrow_6_out_2, n6numrow_to_3numrow_7_out_2, n6numrow_to_3numrow_8_out_2,
       n6numrow_to_3numrow_9_out_2;
  wire [5:0] and_16_out, and_17_out, black1, black2, black3, black4, black5, column1, column2, column3,
       column4, column5, multiplexer_1_out, multiplexer_2_out, multiplexer_3_out, multiplexer_4_out,
       multiplexer_5_out, multiplexer_6_out, multiplexer_7_out, multiplexer_8_out, multiplexer_9_out,
       or_25_out, pull_resistor_3_node, pull_resistor_8_node, pull_resistor_10_node, pull_resistor_11_node,
       shifter_1_out, shifter_2_out, shifter_3_out, shifter_4_out, shifter_5_out, shifter_6_out,
       shifter_7_out, shifter_8_out, shifter_9_out, shifter_10_out, transistor_1_out, transistor_4_out,
       white2, white3, white4, white5;

  or or_1 (or_1_out, _0break_r, _0break_c);
  not not_1 (not_1_out, or_1_out);
  or or_2 (or_2_out, _1break_r, _1break_c);
  not not_2 (not_2_out, or_2_out);
  compare_6bit compare_6bit_1 (.in_1(6'b000001), .in_2(column), .out_3(compare_6bit_1_out_3));
  not not_3 (_0break_c, compare_6bit_1_out_3);
  compare_6bit compare_6bit_2 (.in_1(6'b000001), .in_2(row), .out_3(compare_6bit_2_out_3));
  not not_4 (_0break_r, compare_6bit_2_out_3);
  or or_3 (or_3_out, _3break_r, _3break_c);
  not not_5 (not_5_out, or_3_out);
  or or_4 (or_4_out, _4break_r, _4break_c);
  or or_5 (or_5_out, _2break_r, _2break_c);
  not not_6 (not_6_out, or_5_out);
  not not_7 (not_7_out, or_4_out);
  and and_1 (and_1_out, not_1_out, not_2_out, not_7_out, not_6_out, not_5_out, or_6_out);
  Transistor #(.\type ("n"), .width(6)) transistor_1 (.in(column5), .out(transistor_1_out), .gate(and_1_out));
  assign bit_extender_1_out = {{2{1'b0}}, compare_6bit_1_out_3};  // Bit_Extender bit_extender_1
  assign bit_extender_2_out = {{2{1'b0}}, compare_6bit_2_out_3};  // Bit_Extender bit_extender_2
  or or_6 (or_6_out, _5break_r, _5break_c);
  Pull_Resistor pull_resistor_1 (.node(transistor_1_out));
  or or_7 (or_7_out, _0break_r, _0break_c);
  Shifter #(.width(6), .shift("lr")) shifter_1 (.in(column), .\dist (bit_extender_1_out), .out(shifter_1_out));
  or or_8 (or_8_out, _0break_r, _0break_c);
  Shifter #(.width(6), .shift("lr")) shifter_2 (.in(row), .\dist (bit_extender_2_out), .out(shifter_2_out));
  or or_9 (or_9_out, _1break_r, _1break_c);
  or or_10 (or_10_out, _0break_r, _0break_c);
  not not_8 (not_8_out, or_9_out);
  not not_9 (not_9_out, or_10_out);
  Transistor #(.width(6)) transistor_2 (.in(shifter_1_out), .out(column1), .gate(or_7_out));
  Pull_Resistor pull_resistor_2 (.node(column1));
  Pull_Resistor pull_resistor_3 (.node(pull_resistor_3_node));
  Transistor #(.width(6)) transistor_3 (.in(shifter_2_out), .out(pull_resistor_3_node), .gate(or_8_out));
  _6numRow_to_3numRow u_6numrow_to_3numrow_1 (.in_1(pull_resistor_3_node), .out_2(n6numrow_to_3numrow_1_out_2));
  or or_11 (or_11_out, _4break_r, _4break_c);
  or or_12 (or_12_out, _2break_r, _2break_c);
  not not_10 (not_10_out, or_12_out);
  and and_2 (and_2_out, not_9_out, not_8_out, or_11_out, not_10_out, not_13_out);
  Transistor #(.\type ("n"), .width(6)) transistor_4 (.in(column4), .out(transistor_4_out), .gate(and_2_out));
  Pull_Resistor pull_resistor_4 (.node(transistor_4_out));
  Pull_Resistor pull_resistor_5 (.node(pull_resistor_5_node));
  or or_13 (pull_resistor_5_node, answer2, answer3, answer4, answer5);
  compare_6bit compare_6bit_3 (.in_1(6'b000001), .in_2(column1), .out_3(compare_6bit_3_out_3));
  not not_11 (_1break_c, compare_6bit_3_out_3);
  compare_6bit compare_6bit_4 (.in_1(6'b000001), .in_2(pull_resistor_3_node), .out_3(compare_6bit_4_out_3));
  zero_or_not zero_or_not_1 (.in_1(black1), .out_2(zero_or_not_1_out_2));
  Multiplexer #(.select(3), .width(6)) multiplexer_1 (
    .in0(in_2), .in1(in_4), .in2(in_6), .in3(in_8), .in4(in_10), .in5(in_12), .out(multiplexer_1_out),
    .sel(n6numrow_to_3numrow_1_out_2));  // open: in6, in7, en
  Pull_Resistor pull_resistor_6 (.node(column1));
  or or_14 (or_14_out, _0break_r, _0break_c);
  or or_15 (or_15_out, _3break_r, _3break_c);
  not not_12 (not_12_out, or_14_out);
  not not_13 (not_13_out, or_15_out);
  or or_16 (or_16_out, _0break_c, _0break_r, _1break_c, _1break_r, _2break_c, _2break_r, _3break_c, _3break_r, _4break_c, _4break_r, _5break_c, _5break_r);
  Transistor #(.\type ("n")) transistor_5 (.in(pull_resistor_5_node), .out(out_15), .gate(or_16_out));
  Pull_Resistor pull_resistor_7 (.node(out_15));
  assign bit_extender_3_out = {{2{1'b0}}, compare_6bit_3_out_3};  // Bit_Extender bit_extender_3
  and and_3 (and_3_out, compare_6bit_4_out_3, zero_or_not_1_out_2);
  not not_14 (_1break_r, and_3_out);
  assign black1 = multiplexer_1_out & column1;  // AND_Gate and_4, 6 bits wide
  or or_17 (or_17_out, _1break_r, _1break_c);
  not not_15 (not_15_out, or_17_out);
  or or_18 (or_18_out, _1break_r, _1break_c);
  Shifter #(.width(6), .shift("lr")) shifter_3 (.in(column1), .\dist (bit_extender_3_out), .out(shifter_3_out));
  Shifter #(.width(6), .shift("lr")) shifter_4 (
    .in(pull_resistor_3_node), .\dist (bit_extender_4_out), .out(shifter_4_out));
  assign bit_extender_4_out = {{2{1'b0}}, and_3_out};  // Bit_Extender bit_extender_4
  or or_19 (or_19_out, _2break_r, _2break_c);
  not not_16 (not_16_out, or_19_out);
  or or_20 (or_20_out, _3break_r, _3break_c);
  and and_5 (and_5_out, not_12_out, not_15_out, not_16_out, or_20_out);
  Pull_Resistor pull_resistor_8 (.node(pull_resistor_8_node));
  Transistor #(.\type ("n"), .width(6)) transistor_6 (.in(column3), .out(pull_resistor_8_node), .gate(and_5_out));
  Pull_Resistor pull_resistor_9 (.node(column2));
  Transistor #(.width(6)) transistor_7 (.in(shifter_3_out), .out(column2), .gate(or_18_out));
  or or_21 (or_21_out, _1break_r, _1break_c);
  Pull_Resistor pull_resistor_10 (.node(pull_resistor_10_node));
  Transistor #(.width(6)) transistor_8 (.in(shifter_4_out), .out(pull_resistor_10_node), .gate(or_21_out));
  or or_22 (or_22_out, _0break_r, _0break_c);
  not not_17 (not_17_out, or_22_out);
  compare_6bit compare_6bit_5 (.in_1(6'b000001), .in_2(column2), .out_3(compare_6bit_5_out_3));
  not not_18 (_2break_c, compare_6bit_5_out_3);
  _6numRow_to_3numRow u_6numrow_to_3numrow_2 (.in_1(pull_resistor_10_node), .out_2(n6numrow_to_3numrow_2_out_2));
  Multiplexer #(.select(3), .width(6)) multiplexer_2 (
    .in0(in_2), .in1(in_4), .in2(in_6), .in3(in_8), .in4(in_10), .in5(in_12), .out(multiplexer_2_out),
    .sel(n6numrow_to_3numrow_2_out_2));  // open: in6, in7, en
  _6numRow_to_3numRow u_6numrow_to_3numrow_3 (.in_1(pull_resistor_10_node), .out_2(n6numrow_to_3numrow_3_out_2));
  Multiplexer #(.select(3), .width(6)) multiplexer_3 (
    .in0(in_1), .in1(in_3), .in2(in_5), .in3(in_7), .in4(in_9), .in5(in_11), .out(multiplexer_3_out),
    .sel(n6numrow_to_3numrow_3_out_2));  // open: in6, in7, en
  or or_23 (or_23_out, _1break_r, _1break_c);
  not not_19 (not_19_out, or_23_out);
  or or_24 (or_24_out, _2break_r, _2break_c);
  and and_6 (and_6_out, not_17_out, not_19_out, or_24_out);
  Pull_Resistor pull_resistor_11 (.node(pull_resistor_11_node));
  Transistor #(.\type ("n"), .width(6)) transistor_9 (.in(column2), .out(pull_resistor_11_node), .gate(and_6_out));
  assign bit_extender_5_out = {{2{1'b0}}, compare_6bit_5_out_3};  // Bit_Extender bit_extender_5
  compare_6bit compare_6bit_6 (.in_1(6'b000001), .in_2(pull_resistor_10_node), .out_3(compare_6bit_6_out_3));
  and and_7 (and_7_out, compare_6bit_6_out_3, zero_or_not_2_out_2);
  zero_or_not zero_or_not_2 (.in_1(black2), .out_2(zero_or_not_2_out_2));
  not not_20 (_2break_r, and_7_out);
  Transistor transistor_10 (.in(zero_or_not_3_out_2), .out(answer2), .gate(zero_or_not_2_out_2));
  Pull_Resistor pull_resistor_12 (.node(answer2));
  zero_or_not zero_or_not_3 (.in_1(white2), .out_2(zero_or_not_3_out_2));
  assign black2 = multiplexer_2_out & column2;  // AND_Gate and_8, 6 bits wide
  Pull_Resistor pull_resistor_13 (.node(column2));
  assign white2 = multiplexer_3_out & column2;  // AND_Gate and_9, 6 bits wide
  Pull_Resistor pull_resistor_14 (.node(column2));
  assign or_25_out = pull_resistor_11_node | pull_resistor_8_node | transistor_4_out | transistor_1_out;  // OR_Gate or_25, 6 bits wide
  Shifter #(.width(6), .shift("lr")) shifter_5 (.in(column2), .\dist (bit_extender_5_out), .out(shifter_5_out));
  assign bit_extender_6_out = {{2{1'b0}}, and_7_out};  // Bit_Extender bit_extender_6
  Pull_Resistor pull_resistor_15 (.node(out_col));
  Transistor #(.\type ("n"), .width(6)) transistor_11 (.in(or_25_out), .out(out_col), .gate(out_15));
  or or_26 (or_26_out, _2break_r, _2break_c);
  Pull_Resistor pull_resistor_16 (.node(column3));
  Transistor #(.width(6)) transistor_12 (.in(shifter_5_out), .out(column3), .gate(or_26_out));
  Shifter #(.width(6), .shift("lr")) shifter_6 (
    .in(pull_resistor_10_node), .\dist (bit_extender_6_out), .out(shifter_6_out));
  compare_6bit compare_6bit_7 (.in_1(6'b000001), .in_2(column3), .out_3(compare_6bit_7_out_3));
  not not_21 (_3break_c, compare_6bit_7_out_3);
  _6numRow_to_3numRow u_6numrow_to_3numrow_4 (.in_1(shifter_6_out), .out_2(n6numrow_to_3numrow_4_out_2));
  _6numRow_to_3numRow u_6numrow_to_3numrow_5 (.in_1(shifter_6_out), .out_2(n6numrow_to_3numrow_5_out_2));
  assign bit_extender_7_out = {{2{1'b0}}, compare_6bit_7_out_3};  // Bit_Extender bit_extender_7
  compare_6bit compare_6bit_8 (.in_1(6'b000001), .in_2(shifter_6_out), .out_3(compare_6bit_8_out_3));
  zero_or_not zero_or_not_4 (.in_1(black3), .out_2(zero_or_not_4_out_2));
  zero_or_not zero_or_not_5 (.in_1(white3), .out_2(zero_or_not_5_out_2));
  Multiplexer #(.select(3), .width(6)) multiplexer_4 (
    .in0(in_2), .in1(in_4), .in2(in_6), .in3(in_8), .in4(in_10), .in5(in_12), .out(multiplexer_4_out),
    .sel(n6numrow_to_3numrow_4_out_2));  // open: in6, in7, en
  Pull_Resistor pull_resistor_17 (.node(column3));
  Multiplexer #(.select(3), .width(6)) multiplexer_5 (
    .in0(in_1), .in1(in_3), .in2(in_5), .in3(in_7), .in4(in_9), .in5(in_11), .out(multiplexer_5_out),
    .sel(n6numrow_to_3numrow_5_out_2));  // open: in6, in7, en
  Pull_Resistor pull_resistor_18 (.node(column3));
  Shifter #(.width(6), .shift("lr")) shifter_7 (.in(column3), .\dist (bit_extender_7_out), .out(shifter_7_out));
  and and_10 (and_10_out, compare_6bit_8_out_3, zero_or_not_4_out_2);
  not not_22 (_3break_r, and_10_out);
  Pull_Resistor pull_resistor_19 (.node(answer3));
  Transistor transistor_13 (.in(zero_or_not_5_out_2), .out(answer3), .gate(zero_or_not_4_out_2));
  assign black3 = multiplexer_4_out & column3;  // AND_Gate and_11, 6 bits wide
  assign white3 = multiplexer_5_out & column3;  // AND_Gate and_12, 6 bits wide
  or or_27 (or_27_out, _3break_r, _3break_c);
  Transistor #(.width(6)) transistor_14 (.in(shifter_7_out), .out(column4), .gate(or_27_out));
  Pull_Resistor pull_resistor_20 (.node(column4));
  Shifter #(.width(6), .shift("lr")) shifter_8 (.in(shifter_6_out), .\dist (bit_extender_8_out), .out(shifter_8_out));
  assign bit_extender_8_out = {{2{1'b0}}, and_10_out};  // Bit_Extender bit_extender_8
  compare_6bit compare_6bit_9 (.in_1(6'b000001), .in_2(column4), .out_3(compare_6bit_9_out_3));
  not not_23 (_4break_c, compare_6bit_9_out_3);
  assign bit_extender_9_out = {{2{1'b0}}, compare_6bit_9_out_3};  // Bit_Extender bit_extender_9
  _6numRow_to_3numRow u_6numrow_to_3numrow_6 (.in_1(shifter_8_out), .out_2(n6numrow_to_3numrow_6_out_2));
  Multiplexer #(.select(3), .width(6)) multiplexer_6 (
    .in0(in_2), .in1(in_4), .in2(in_6), .in3(in_8), .in4(in_10), .in5(in_12), .out(multiplexer_6_out),
    .sel(n6numrow_to_3numrow_6_out_2));  // open: in6, in7, en
  _6numRow_to_3numRow u_6numrow_to_3numrow_7 (.in_1(shifter_8_out), .out_2(n6numrow_to_3numrow_7_out_2));
  Multiplexer #(.select(3), .width(6)) multiplexer_7 (
    .in0(in_1), .in1(in_3), .in2(in_5), .in3(in_7), .in4(in_9), .in5(in_11), .out(multiplexer_7_out),
    .sel(n6numrow_to_3numrow_7_out_2));  // open: in6, in7, en
  Shifter #(.width(6), .shift("lr")) shifter_9 (.in(column4), .\dist (bit_extender_9_out), .out(shifter_9_out));
  compare_6bit compare_6bit_10 (.in_1(6'b000001), .in_2(shifter_8_out), .out_3(compare_6bit_10_out_3));
  and and_13 (and_13_out, compare_6bit_10_out_3, zero_or_not_6_out_2);
  not not_24 (_4break_r, and_13_out);
  zero_or_not zero_or_not_6 (.in_1(black4), .out_2(zero_or_not_6_out_2));
  Pull_Resistor pull_resistor_21 (.node(answer4));
  Transistor transistor_15 (.in(zero_or_not_7_out_2), .out(answer4), .gate(zero_or_not_6_out_2));
  zero_or_not zero_or_not_7 (.in_1(white4), .out_2(zero_or_not_7_out_2));
  assign black4 = multiplexer_6_out & column4;  // AND_Gate and_14, 6 bits wide
  Pull_Resistor pull_resistor_22 (.node(column4));
  assign white4 = multiplexer_7_out & column4;  // AND_Gate and_15, 6 bits wide
  Pull_Resistor pull_resistor_23 (.node(column4));
  or or_28 (or_28_out, _4break_r, _4break_c);
  Pull_Resistor pull_resistor_24 (.node(column5));
  Transistor #(.width(6)) transistor_16 (.in(shifter_9_out), .out(column5), .gate(or_28_out));
  assign bit_extender_10_out = {{2{1'b0}}, and_13_out};  // Bit_Extender bit_extender_10
  compare_6bit compare_6bit_11 (.in_1(6'b000001), .in_2(column5), .out_3(compare_6bit_11_out_3));
  Shifter #(.width(6), .shift("lr")) shifter_10 (
    .in(shifter_8_out), .\dist (bit_extender_10_out), .out(shifter_10_out));
  _6numRow_to_3numRow u_6numrow_to_3numrow_8 (.in_1(shifter_10_out), .out_2(n6numrow_to_3numrow_8_out_2));
  _6numRow_to_3numRow u_6numrow_to_3numrow_9 (.in_1(shifter_10_out), .out_2(n6numrow_to_3numrow_9_out_2));
  not not_25 (_5break_c, compare_6bit_11_out_3);
  zero_or_not zero_or_not_8 (.in_1(and_16_out), .out_2(zero_or_not_8_out_2));
  assign and_16_out = shifter_10_out & black5;  // AND_Gate and_16, 6 bits wide
  zero_or_not zero_or_not_9 (.in_1(and_17_out), .out_2(answer5));
  assign and_17_out = shifter_10_out & white5;  // AND_Gate and_17, 6 bits wide
  Multiplexer #(.select(3), .width(6)) multiplexer_8 (
    .in0(in_2), .in1(in_4), .in2(in_6), .in3(in_8), .in4(in_10), .in5(in_12), .out(multiplexer_8_out),
    .sel(n6numrow_to_3numrow_8_out_2));  // open: in6, in7, en
  Pull_Resistor pull_resistor_25 (.node(column5));
  Multiplexer #(.select(3), .width(6)) multiplexer_9 (
    .in0(in_1), .in1(in_3), .in2(in_5), .in3(in_7), .in4(in_9), .in5(in_11), .out(multiplexer_9_out),
    .sel(n6numrow_to_3numrow_9_out_2));  // open: in6, in7, en
  Pull_Resistor pull_resistor_26 (.node(column5));
  not not_26 (_5break_r, zero_or_not_8_out_2);
  assign black5 = multiplexer_8_out & column5;  // AND_Gate and_18, 6 bits wide
  assign white5 = multiplexer_9_out & column5;  // AND_Gate and_19, 6 bits wide

  // Other names for the same wires on the sheet: _0b[5:0] = in_2; _0w[5:0] = in_1; _1b[5:0] = in_4; _1w[5:0] = in_3;
  //   _2b[5:0] = in_6; _2w[5:0] = in_5; _3b[5:0] = in_8; _3w[5:0] = in_7; _4b[5:0] = in_10; _4w[5:0] = in_9;
  //   _5b[5:0] = in_12; _5w[5:0] = in_11; fin_answer = out_15
endmodule

module check_diag_rd (
  input  [5:0] in_1,
  input  [5:0] in_2,
  input  [5:0] in_3,
  input  [5:0] in_4,
  input  [5:0] in_5,
  input  [5:0] in_6,
  input  [5:0] in_7,
  input  [5:0] in_8,
  input  [5:0] in_9,
  input  [5:0] in_10,
  input  [5:0] in_11,
  input  [5:0] in_12,
  input  [5:0] column,
  input  [5:0] row,
  output out_15,
  output [5:0] out_col
);

  wire _0break_c, _0break_r, _1break_c, _1break_r, _2break_c, _2break_r, _3break_c, _3break_r, _4break_c,
       _4break_r, _5break_c, _5break_r, and_1_out, and_2_out, and_3_out, and_5_out, and_6_out, and_7_out,
       and_10_out, and_13_out, answer2, answer3, answer4, answer5, compare_6bit_1_out_3,
       compare_6bit_2_out_3, compare_6bit_3_out_3, compare_6bit_4_out_3, compare_6bit_5_out_3,
       compare_6bit_6_out_3, compare_6bit_7_out_3, compare_6bit_8_out_3, compare_6bit_9_out_3,
       compare_6bit_10_out_3, compare_6bit_11_out_3, not_1_out, not_2_out, not_5_out, not_6_out, not_7_out,
       not_8_out, not_9_out, not_10_out, not_12_out, not_13_out, not_15_out, not_16_out, not_17_out,
       not_19_out, or_1_out, or_2_out, or_3_out, or_4_out, or_5_out, or_6_out, or_7_out, or_8_out, or_9_out,
       or_10_out, or_11_out, or_12_out, or_14_out, or_15_out, or_16_out, or_17_out, or_18_out, or_19_out,
       or_20_out, or_21_out, or_22_out, or_23_out, or_24_out, or_26_out, or_27_out, or_28_out,
       pull_resistor_5_node, zero_or_not_1_out_2, zero_or_not_2_out_2, zero_or_not_3_out_2,
       zero_or_not_4_out_2, zero_or_not_5_out_2, zero_or_not_6_out_2, zero_or_not_7_out_2,
       zero_or_not_8_out_2;
  wire [2:0] bit_extender_1_out, bit_extender_2_out, bit_extender_3_out, bit_extender_4_out,
       bit_extender_5_out, bit_extender_6_out, bit_extender_7_out, bit_extender_8_out, bit_extender_9_out,
       bit_extender_10_out, n6numrow_to_3numrow_1_out_2, n6numrow_to_3numrow_2_out_2,
       n6numrow_to_3numrow_3_out_2, n6numrow_to_3numrow_4_out_2, n6numrow_to_3numrow_5_out_2,
       n6numrow_to_3numrow_6_out_2, n6numrow_to_3numrow_7_out_2, n6numrow_to_3numrow_8_out_2,
       n6numrow_to_3numrow_9_out_2;
  wire [5:0] and_16_out, and_17_out, black1, black2, black3, black4, black5, column1, column2, column3,
       column4, column5, multiplexer_1_out, multiplexer_2_out, multiplexer_3_out, multiplexer_4_out,
       multiplexer_5_out, multiplexer_6_out, multiplexer_7_out, multiplexer_8_out, multiplexer_9_out,
       or_25_out, pull_resistor_3_node, pull_resistor_10_node, shifter_1_out, shifter_2_out, shifter_3_out,
       shifter_4_out, shifter_5_out, shifter_6_out, shifter_7_out, shifter_8_out, shifter_9_out,
       shifter_10_out, transistor_1_out, transistor_4_out, transistor_6_out, transistor_9_out, white2,
       white3, white4, white5;

  or or_1 (or_1_out, _0break_r, _0break_c);
  not not_1 (not_1_out, or_1_out);
  or or_2 (or_2_out, _1break_r, _1break_c);
  not not_2 (not_2_out, or_2_out);
  compare_6bit compare_6bit_1 (.in_1(6'b000001), .in_2(column), .out_3(compare_6bit_1_out_3));
  not not_3 (_0break_c, compare_6bit_1_out_3);
  compare_6bit compare_6bit_2 (.in_1(6'b100000), .in_2(row), .out_3(compare_6bit_2_out_3));
  not not_4 (_0break_r, compare_6bit_2_out_3);
  or or_3 (or_3_out, _3break_r, _3break_c);
  not not_5 (not_5_out, or_3_out);
  or or_4 (or_4_out, _4break_r, _4break_c);
  or or_5 (or_5_out, _2break_r, _2break_c);
  not not_6 (not_6_out, or_5_out);
  not not_7 (not_7_out, or_4_out);
  and and_1 (and_1_out, not_1_out, not_2_out, not_7_out, not_6_out, not_5_out, or_6_out);
  Transistor #(.\type ("n"), .width(6)) transistor_1 (.in(column5), .out(transistor_1_out), .gate(and_1_out));
  assign bit_extender_1_out = {{2{1'b0}}, compare_6bit_1_out_3};  // Bit_Extender bit_extender_1
  assign bit_extender_2_out = {{2{1'b0}}, compare_6bit_2_out_3};  // Bit_Extender bit_extender_2
  or or_6 (or_6_out, _5break_r, _5break_c);
  Pull_Resistor pull_resistor_1 (.node(transistor_1_out));
  or or_7 (or_7_out, _0break_r, _0break_c);
  Shifter #(.width(6), .shift("lr")) shifter_1 (.in(column), .\dist (bit_extender_1_out), .out(shifter_1_out));
  or or_8 (or_8_out, _0break_r, _0break_c);
  Shifter #(.width(6)) shifter_2 (.in(row), .\dist (bit_extender_2_out), .out(shifter_2_out));
  or or_9 (or_9_out, _1break_r, _1break_c);
  or or_10 (or_10_out, _0break_r, _0break_c);
  not not_8 (not_8_out, or_9_out);
  not not_9 (not_9_out, or_10_out);
  Transistor #(.width(6)) transistor_2 (.in(shifter_1_out), .out(column1), .gate(or_7_out));
  Pull_Resistor pull_resistor_2 (.node(column1));
  Pull_Resistor pull_resistor_3 (.node(pull_resistor_3_node));
  Transistor #(.width(6)) transistor_3 (.in(shifter_2_out), .out(pull_resistor_3_node), .gate(or_8_out));
  _6numRow_to_3numRow u_6numrow_to_3numrow_1 (.in_1(pull_resistor_3_node), .out_2(n6numrow_to_3numrow_1_out_2));
  or or_11 (or_11_out, _4break_r, _4break_c);
  or or_12 (or_12_out, _2break_r, _2break_c);
  not not_10 (not_10_out, or_12_out);
  and and_2 (and_2_out, not_9_out, not_8_out, or_11_out, not_10_out, not_13_out);
  Transistor #(.\type ("n"), .width(6)) transistor_4 (.in(column4), .out(transistor_4_out), .gate(and_2_out));
  Pull_Resistor pull_resistor_4 (.node(transistor_4_out));
  Pull_Resistor pull_resistor_5 (.node(pull_resistor_5_node));
  or or_13 (pull_resistor_5_node, answer2, answer3, answer4, answer5);
  compare_6bit compare_6bit_3 (.in_1(6'b000001), .in_2(column1), .out_3(compare_6bit_3_out_3));
  not not_11 (_1break_c, compare_6bit_3_out_3);
  compare_6bit compare_6bit_4 (.in_1(6'b100000), .in_2(pull_resistor_3_node), .out_3(compare_6bit_4_out_3));
  zero_or_not zero_or_not_1 (.in_1(black1), .out_2(zero_or_not_1_out_2));
  Multiplexer #(.select(3), .width(6)) multiplexer_1 (
    .in0(in_2), .in1(in_4), .in2(in_6), .in3(in_8), .in4(in_10), .in5(in_12), .out(multiplexer_1_out),
    .sel(n6numrow_to_3numrow_1_out_2));  // open: in6, in7, en
  Pull_Resistor pull_resistor_6 (.node(column1));
  or or_14 (or_14_out, _0break_r, _0break_c);
  not not_12 (not_12_out, or_14_out);
  or or_15 (or_15_out, _3break_r, _3break_c);
  not not_13 (not_13_out, or_15_out);
  or or_16 (or_16_out, _0break_c, _0break_r, _1break_c, _1break_r, _2break_c, _2break_r, _3break_c, _3break_r, _4break_c, _4break_r, _5break_c, _5break_r);
  Pull_Resistor pull_resistor_7 (.node(out_15));
  Transistor #(.\type ("n")) transistor_5 (.in(pull_resistor_5_node), .out(out_15), .gate(or_16_out));
  assign bit_extender_3_out = {{2{1'b0}}, compare_6bit_3_out_3};  // Bit_Extender bit_extender_3
  and and_3 (and_3_out, compare_6bit_4_out_3, zero_or_not_1_out_2);
  not not_14 (_1break_r, and_3_out);
  assign black1 = multiplexer_1_out & column1;  // AND_Gate and_4, 6 bits wide
  or or_17 (or_17_out, _1break_r, _1break_c);
  not not_15 (not_15_out, or_17_out);
  or or_18 (or_18_out, _1break_r, _1break_c);
  Shifter #(.width(6), .shift("lr")) shifter_3 (.in(column1), .\dist (bit_extender_3_out), .out(shifter_3_out));
  Shifter #(.width(6)) shifter_4 (.in(pull_resistor_3_node), .\dist (bit_extender_4_out), .out(shifter_4_out));
  assign bit_extender_4_out = {{2{1'b0}}, and_3_out};  // Bit_Extender bit_extender_4
  or or_19 (or_19_out, _2break_r, _2break_c);
  not not_16 (not_16_out, or_19_out);
  or or_20 (or_20_out, _3break_r, _3break_c);
  and and_5 (and_5_out, not_12_out, not_15_out, not_16_out, or_20_out);
  Transistor #(.\type ("n"), .width(6)) transistor_6 (.in(column3), .out(transistor_6_out), .gate(and_5_out));
  Pull_Resistor pull_resistor_8 (.node(transistor_6_out));
  Transistor #(.width(6)) transistor_7 (.in(shifter_3_out), .out(column2), .gate(or_18_out));
  Pull_Resistor pull_resistor_9 (.node(column2));
  or or_21 (or_21_out, _1break_r, _1break_c);
  Pull_Resistor pull_resistor_10 (.node(pull_resistor_10_node));
  Transistor #(.width(6)) transistor_8 (.in(shifter_4_out), .out(pull_resistor_10_node), .gate(or_21_out));
  or or_22 (or_22_out, _0break_r, _0break_c);
  not not_17 (not_17_out, or_22_out);
  compare_6bit compare_6bit_5 (.in_1(6'b000001), .in_2(column2), .out_3(compare_6bit_5_out_3));
  not not_18 (_2break_c, compare_6bit_5_out_3);
  _6numRow_to_3numRow u_6numrow_to_3numrow_2 (.in_1(pull_resistor_10_node), .out_2(n6numrow_to_3numrow_2_out_2));
  Multiplexer #(.select(3), .width(6)) multiplexer_2 (
    .in0(in_2), .in1(in_4), .in2(in_6), .in3(in_8), .in4(in_10), .in5(in_12), .out(multiplexer_2_out),
    .sel(n6numrow_to_3numrow_2_out_2));  // open: in6, in7, en
  _6numRow_to_3numRow u_6numrow_to_3numrow_3 (.in_1(pull_resistor_10_node), .out_2(n6numrow_to_3numrow_3_out_2));
  Multiplexer #(.select(3), .width(6)) multiplexer_3 (
    .in0(in_1), .in1(in_3), .in2(in_5), .in3(in_7), .in4(in_9), .in5(in_11), .out(multiplexer_3_out),
    .sel(n6numrow_to_3numrow_3_out_2));  // open: in6, in7, en
  or or_23 (or_23_out, _1break_r, _1break_c);
  not not_19 (not_19_out, or_23_out);
  or or_24 (or_24_out, _2break_r, _2break_c);
  and and_6 (and_6_out, not_17_out, not_19_out, or_24_out);
  Transistor #(.\type ("n"), .width(6)) transistor_9 (.in(column2), .out(transistor_9_out), .gate(and_6_out));
  Pull_Resistor pull_resistor_11 (.node(transistor_9_out));
  assign bit_extender_5_out = {{2{1'b0}}, compare_6bit_5_out_3};  // Bit_Extender bit_extender_5
  compare_6bit compare_6bit_6 (.in_1(6'b100000), .in_2(pull_resistor_10_node), .out_3(compare_6bit_6_out_3));
  and and_7 (and_7_out, compare_6bit_6_out_3, zero_or_not_2_out_2);
  not not_20 (_2break_r, and_7_out);
  zero_or_not zero_or_not_2 (.in_1(black2), .out_2(zero_or_not_2_out_2));
  Pull_Resistor pull_resistor_12 (.node(answer2));
  zero_or_not zero_or_not_3 (.in_1(white2), .out_2(zero_or_not_3_out_2));
  Transistor transistor_10 (.in(zero_or_not_3_out_2), .out(answer2), .gate(zero_or_not_2_out_2));
  assign black2 = multiplexer_2_out & column2;  // AND_Gate and_8, 6 bits wide
  Pull_Resistor pull_resistor_13 (.node(column2));
  assign white2 = multiplexer_3_out & column2;  // AND_Gate and_9, 6 bits wide
  Pull_Resistor pull_resistor_14 (.node(column2));
  assign or_25_out = transistor_9_out | transistor_6_out | transistor_4_out | transistor_1_out;  // OR_Gate or_25, 6 bits wide
  Shifter #(.width(6), .shift("lr")) shifter_5 (.in(column2), .\dist (bit_extender_5_out), .out(shifter_5_out));
  assign bit_extender_6_out = {{2{1'b0}}, and_7_out};  // Bit_Extender bit_extender_6
  Pull_Resistor pull_resistor_15 (.node(out_col));
  Transistor #(.\type ("n"), .width(6)) transistor_11 (.in(or_25_out), .out(out_col), .gate(out_15));
  or or_26 (or_26_out, _2break_r, _2break_c);
  Transistor #(.width(6)) transistor_12 (.in(shifter_5_out), .out(column3), .gate(or_26_out));
  Pull_Resistor pull_resistor_16 (.node(column3));
  Shifter #(.width(6)) shifter_6 (.in(pull_resistor_10_node), .\dist (bit_extender_6_out), .out(shifter_6_out));
  compare_6bit compare_6bit_7 (.in_1(6'b000001), .in_2(column3), .out_3(compare_6bit_7_out_3));
  not not_21 (_3break_c, compare_6bit_7_out_3);
  _6numRow_to_3numRow u_6numrow_to_3numrow_4 (.in_1(shifter_6_out), .out_2(n6numrow_to_3numrow_4_out_2));
  _6numRow_to_3numRow u_6numrow_to_3numrow_5 (.in_1(shifter_6_out), .out_2(n6numrow_to_3numrow_5_out_2));
  assign bit_extender_7_out = {{2{1'b0}}, compare_6bit_7_out_3};  // Bit_Extender bit_extender_7
  compare_6bit compare_6bit_8 (.in_1(6'b100000), .in_2(shifter_6_out), .out_3(compare_6bit_8_out_3));
  zero_or_not zero_or_not_4 (.in_1(black3), .out_2(zero_or_not_4_out_2));
  zero_or_not zero_or_not_5 (.in_1(white3), .out_2(zero_or_not_5_out_2));
  Multiplexer #(.select(3), .width(6)) multiplexer_4 (
    .in0(in_2), .in1(in_4), .in2(in_6), .in3(in_8), .in4(in_10), .in5(in_12), .out(multiplexer_4_out),
    .sel(n6numrow_to_3numrow_4_out_2));  // open: in6, in7, en
  Pull_Resistor pull_resistor_17 (.node(column3));
  Multiplexer #(.select(3), .width(6)) multiplexer_5 (
    .in0(in_1), .in1(in_3), .in2(in_5), .in3(in_7), .in4(in_9), .in5(in_11), .out(multiplexer_5_out),
    .sel(n6numrow_to_3numrow_5_out_2));  // open: in6, in7, en
  Pull_Resistor pull_resistor_18 (.node(column3));
  Shifter #(.width(6), .shift("lr")) shifter_7 (.in(column3), .\dist (bit_extender_7_out), .out(shifter_7_out));
  and and_10 (and_10_out, compare_6bit_8_out_3, zero_or_not_4_out_2);
  not not_22 (_3break_r, and_10_out);
  Transistor transistor_13 (.in(zero_or_not_5_out_2), .out(answer3), .gate(zero_or_not_4_out_2));
  Pull_Resistor pull_resistor_19 (.node(answer3));
  assign black3 = multiplexer_4_out & column3;  // AND_Gate and_11, 6 bits wide
  assign white3 = multiplexer_5_out & column3;  // AND_Gate and_12, 6 bits wide
  or or_27 (or_27_out, _3break_r, _3break_c);
  Pull_Resistor pull_resistor_20 (.node(column4));
  Transistor #(.width(6)) transistor_14 (.in(shifter_7_out), .out(column4), .gate(or_27_out));
  Shifter #(.width(6)) shifter_8 (.in(shifter_6_out), .\dist (bit_extender_8_out), .out(shifter_8_out));
  assign bit_extender_8_out = {{2{1'b0}}, and_10_out};  // Bit_Extender bit_extender_8
  compare_6bit compare_6bit_9 (.in_1(6'b000001), .in_2(column4), .out_3(compare_6bit_9_out_3));
  not not_23 (_4break_c, compare_6bit_9_out_3);
  assign bit_extender_9_out = {{2{1'b0}}, compare_6bit_9_out_3};  // Bit_Extender bit_extender_9
  _6numRow_to_3numRow u_6numrow_to_3numrow_6 (.in_1(shifter_8_out), .out_2(n6numrow_to_3numrow_6_out_2));
  Multiplexer #(.select(3), .width(6)) multiplexer_6 (
    .in0(in_2), .in1(in_4), .in2(in_6), .in3(in_8), .in4(in_10), .in5(in_12), .out(multiplexer_6_out),
    .sel(n6numrow_to_3numrow_6_out_2));  // open: in6, in7, en
  _6numRow_to_3numRow u_6numrow_to_3numrow_7 (.in_1(shifter_8_out), .out_2(n6numrow_to_3numrow_7_out_2));
  Multiplexer #(.select(3), .width(6)) multiplexer_7 (
    .in0(in_1), .in1(in_3), .in2(in_5), .in3(in_7), .in4(in_9), .in5(in_11), .out(multiplexer_7_out),
    .sel(n6numrow_to_3numrow_7_out_2));  // open: in6, in7, en
  Shifter #(.width(6), .shift("lr")) shifter_9 (.in(column4), .\dist (bit_extender_9_out), .out(shifter_9_out));
  compare_6bit compare_6bit_10 (.in_1(6'b100000), .in_2(shifter_8_out), .out_3(compare_6bit_10_out_3));
  and and_13 (and_13_out, compare_6bit_10_out_3, zero_or_not_6_out_2);
  not not_24 (_4break_r, and_13_out);
  zero_or_not zero_or_not_6 (.in_1(black4), .out_2(zero_or_not_6_out_2));
  zero_or_not zero_or_not_7 (.in_1(white4), .out_2(zero_or_not_7_out_2));
  Pull_Resistor pull_resistor_21 (.node(answer4));
  Transistor transistor_15 (.in(zero_or_not_7_out_2), .out(answer4), .gate(zero_or_not_6_out_2));
  assign black4 = multiplexer_6_out & column4;  // AND_Gate and_14, 6 bits wide
  Pull_Resistor pull_resistor_22 (.node(column4));
  assign white4 = multiplexer_7_out & column4;  // AND_Gate and_15, 6 bits wide
  Pull_Resistor pull_resistor_23 (.node(column4));
  or or_28 (or_28_out, _4break_r, _4break_c);
  Transistor #(.width(6)) transistor_16 (.in(shifter_9_out), .out(column5), .gate(or_28_out));
  Pull_Resistor pull_resistor_24 (.node(column5));
  assign bit_extender_10_out = {{2{1'b0}}, and_13_out};  // Bit_Extender bit_extender_10
  compare_6bit compare_6bit_11 (.in_1(6'b000001), .in_2(column5), .out_3(compare_6bit_11_out_3));
  Shifter #(.width(6)) shifter_10 (.in(shifter_8_out), .\dist (bit_extender_10_out), .out(shifter_10_out));
  _6numRow_to_3numRow u_6numrow_to_3numrow_8 (.in_1(shifter_10_out), .out_2(n6numrow_to_3numrow_8_out_2));
  _6numRow_to_3numRow u_6numrow_to_3numrow_9 (.in_1(shifter_10_out), .out_2(n6numrow_to_3numrow_9_out_2));
  not not_25 (_5break_c, compare_6bit_11_out_3);
  zero_or_not zero_or_not_8 (.in_1(and_16_out), .out_2(zero_or_not_8_out_2));
  assign and_16_out = shifter_10_out & black5;  // AND_Gate and_16, 6 bits wide
  assign and_17_out = shifter_10_out & white5;  // AND_Gate and_17, 6 bits wide
  zero_or_not zero_or_not_9 (.in_1(and_17_out), .out_2(answer5));
  Multiplexer #(.select(3), .width(6)) multiplexer_8 (
    .in0(in_2), .in1(in_4), .in2(in_6), .in3(in_8), .in4(in_10), .in5(in_12), .out(multiplexer_8_out),
    .sel(n6numrow_to_3numrow_8_out_2));  // open: in6, in7, en
  Pull_Resistor pull_resistor_25 (.node(column5));
  Multiplexer #(.select(3), .width(6)) multiplexer_9 (
    .in0(in_1), .in1(in_3), .in2(in_5), .in3(in_7), .in4(in_9), .in5(in_11), .out(multiplexer_9_out),
    .sel(n6numrow_to_3numrow_9_out_2));  // open: in6, in7, en
  Pull_Resistor pull_resistor_26 (.node(column5));
  not not_26 (_5break_r, zero_or_not_8_out_2);
  assign black5 = multiplexer_8_out & column5;  // AND_Gate and_18, 6 bits wide
  assign white5 = multiplexer_9_out & column5;  // AND_Gate and_19, 6 bits wide

  // Other names for the same wires on the sheet: _0b[5:0] = in_2; _0w[5:0] = in_1; _1b[5:0] = in_4; _1w[5:0] = in_3;
  //   _2b[5:0] = in_6; _2w[5:0] = in_5; _3b[5:0] = in_8; _3w[5:0] = in_7; _4b[5:0] = in_10; _4w[5:0] = in_9;
  //   _5b[5:0] = in_12; _5w[5:0] = in_11; fin_answer = out_15
endmodule
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module row_to_column_for_black (
  input  [5:0] column_black,
  input  [5:0] column_num,
  output [5:0] out_3,
  output [5:0] out_4,
  output [5:0] out_5,
  output [5:0] out_6,
  output [5:0] out_7,
  output [5:0] out_8
);

  wire [5:0] nor_1_out, nor_2_out, nor_3_out, nor_4_out, nor_5_out, nor_6_out;

  assign nor_1_out = ~(column_num | {6{1'b0}});  // NOR_Gate nor_1, 6 bits wide
  assign nor_2_out = ~(column_num | {6{1'b0}});  // NOR_Gate nor_2, 6 bits wide
  assign nor_3_out = ~(column_num | {6{1'b0}});  // NOR_Gate nor_3, 6 bits wide
  assign nor_4_out = ~(column_num | {6{1'b0}});  // NOR_Gate nor_4, 6 bits wide
  assign nor_5_out = ~(column_num | {6{1'b0}});  // NOR_Gate nor_5, 6 bits wide
  assign nor_6_out = ~(column_num | {6{1'b0}});  // NOR_Gate nor_6, 6 bits wide
  if_6bit if_6bit_1 (.Input_0(nor_1_out), .sel(column_black[0]), .Input_1({6{1'b1}}), .Output(out_3));
  if_6bit if_6bit_2 (.Input_0(nor_2_out), .sel(column_black[1]), .Input_1({6{1'b1}}), .Output(out_4));
  if_6bit if_6bit_3 (.Input_0(nor_3_out), .sel(column_black[2]), .Input_1({6{1'b1}}), .Output(out_5));
  if_6bit if_6bit_4 (.Input_0(nor_4_out), .sel(column_black[3]), .Input_1({6{1'b1}}), .Output(out_6));
  if_6bit if_6bit_5 (.Input_0(nor_5_out), .sel(column_black[4]), .Input_1({6{1'b1}}), .Output(out_7));
  if_6bit if_6bit_6 (.Input_0(nor_6_out), .sel(column_black[5]), .Input_1({6{1'b1}}), .Output(out_8));

  // Other names for the same wires on the sheet: c_n[5:0] = column_num
endmodule

module E_to_one_6bit (
  input  [5:0] in_1,
  output [5:0] out_2
);

  E_to_one_1bit e_to_one_1bit_1 (.in_1(in_1[0]), .out_2(out_2[0]));
  E_to_one_1bit e_to_one_1bit_2 (.in_1(in_1[1]), .out_2(out_2[1]));
  E_to_one_1bit e_to_one_1bit_3 (.in_1(in_1[2]), .out_2(out_2[2]));
  E_to_one_1bit e_to_one_1bit_4 (.in_1(in_1[3]), .out_2(out_2[3]));
  E_to_one_1bit e_to_one_1bit_5 (.in_1(in_1[4]), .out_2(out_2[4]));
  E_to_one_1bit e_to_one_1bit_6 (.in_1(in_1[5]), .out_2(out_2[5]));
endmodule

module E_to_one_1bit (
  input  in_1,
  output out_2
);

  wire and_1_out, and_2_out, and_3_out, bitselector_1_out, bitselector_2_out, buffer_1_out, buffer_2_out,
       buffer_3_out, buffer_4_out, buffer_5_out, buffer_6_out;

  buf buffer_1 (buffer_1_out, in_1);
  buf buffer_2 (buffer_2_out, in_1);
  Pull_Resistor #(.pull(1)) pull_resistor_1 (.node(buffer_2_out));
  BitSelector #(.width(1)) bitselector_1 (.in(1'b0), .out(bitselector_1_out), .sel(in_1));
  buf buffer_3 (buffer_3_out, bitselector_1_out);
  buf buffer_4 (buffer_4_out, bitselector_1_out);
  buf buffer_5 (buffer_5_out, bitselector_2_out);
  BitSelector #(.width(1)) bitselector_2 (.out(bitselector_2_out), .sel(and_1_out));  // open: in
  buf buffer_6 (buffer_6_out, bitselector_2_out);
  and and_1 (and_1_out, ~buffer_1_out, buffer_2_out);  // AND_Gate
  Pull_Resistor pull_resistor_2 (.node(buffer_3_out));
  and and_2 (and_2_out, ~buffer_3_out, buffer_4_out);  // AND_Gate
  Pull_Resistor #(.pull(1)) pull_resistor_3 (.node(buffer_4_out));
  Pull_Resistor pull_resistor_4 (.node(buffer_5_out));
  and and_3 (and_3_out, ~buffer_5_out, buffer_6_out);  // AND_Gate
  Pull_Resistor #(.pull(1)) pull_resistor_5 (.node(buffer_6_out));
  and and_4 (out_2, and_2_out, and_3_out);
endmodule

module game_over (
  input  [5:0] in_1,
  input  [5:0] in_2,
  output white_win,
  output draw,
  output black_win,
  output game_over
);

  wire comparator_1_eq, comparator_1_gt, comparator_1_lt;
  wire [5:0] adder_1_out;

  Adder #(.width(6)) adder_1 (.a(in_1), .b(in_2), .out(adder_1_out));  // open: cin, cout
  Pull_Resistor pull_resistor_1 (.node(white_win));
  Transistor #(.\type ("n")) transistor_1 (.in(comparator_1_gt), .out(white_win), .gate(game_over));
  Comparator #(.width(6), .mode("unsigned")) comparator_1 (
    .a(in_1), .b(in_2), .gt(comparator_1_gt), .eq(comparator_1_eq), .lt(comparator_1_lt));
  Transistor #(.\type ("n")) transistor_2 (.in(comparator_1_eq), .out(draw), .gate(game_over));
  Pull_Resistor pull_resistor_2 (.node(draw));
  Transistor #(.\type ("n")) transistor_3 (.in(comparator_1_lt), .out(black_win), .gate(game_over));
  Pull_Resistor pull_resistor_3 (.node(black_win));
  Comparator #(.width(6), .mode("unsigned")) comparator_2 (
    .a(adder_1_out), .b(6'b100100), .eq(game_over));  // open: gt, lt
endmodule
